// Logisim project Arcade.circ as structural Verilog: 19 circuits, main circuit Lacascade
module Lacascade (
);

  wire button_1_out, button_2_out, button_3_out, button_4_out, Start_out, verlaine_1_out_7;
  wire [3:0] verlaine_1_out_3, verlaine_1_out_4, verlaine_1_out_5, verlaine_1_out_6;
  wire [9:0] jean_paul_sat_1_out_6, jean_paul_sat_1_out_7, jean_paul_sat_1_out_8, jean_paul_sat_1_out_9,
       jean_paul_sat_1_out_10, jean_paul_sat_1_out_11, jean_paul_sat_1_out_12, jean_paul_sat_1_out_14,
       jean_paul_sat_1_out_15, jean_paul_sat_1_out_16, jean_paul_sat_1_out_17, jean_paul_sat_1_out_18,
       jean_paul_sat_1_out_19, jean_paul_sat_1_out_20, jean_paul_sat_1_out_21, jean_paul_sat_1_out_22,
       jean_paul_sat_1_out_23, jean_paul_sat_1_out_24, jean_paul_sat_1_out_25, jean_paul_sat_1_out_26;
  wire [15:0] jean_paul_sat_1_out_13;

  Hex_Digit_Display hex_digit_display_1 (.value(verlaine_1_out_3));  // open: dp
  Verlaine verlaine_1 (
    .in_1(jean_paul_sat_1_out_13), .out_3(verlaine_1_out_3), .out_4(verlaine_1_out_4),
    .out_5(verlaine_1_out_5), .out_6(verlaine_1_out_6), .out_7(verlaine_1_out_7), .in_2(Start_out));
  Jean_Paul_SAT jean_paul_sat_1 (
    .out_6(jean_paul_sat_1_out_6), .out_7(jean_paul_sat_1_out_7), .out_8(jean_paul_sat_1_out_8),
    .out_9(jean_paul_sat_1_out_9), .out_10(jean_paul_sat_1_out_10), .out_11(jean_paul_sat_1_out_11),
    .out_12(jean_paul_sat_1_out_12), .out_14(jean_paul_sat_1_out_14), .out_15(jean_paul_sat_1_out_15),
    .out_16(jean_paul_sat_1_out_16), .out_17(jean_paul_sat_1_out_17), .out_18(jean_paul_sat_1_out_18),
    .out_19(jean_paul_sat_1_out_19), .out_20(jean_paul_sat_1_out_20), .out_21(jean_paul_sat_1_out_21),
    .out_22(jean_paul_sat_1_out_22), .out_23(jean_paul_sat_1_out_23), .out_24(jean_paul_sat_1_out_24),
    .out_25(jean_paul_sat_1_out_25), .out_26(jean_paul_sat_1_out_26), .in_2(button_2_out),
    .in_3(button_1_out), .in_4(button_4_out), .in_5(button_3_out), .in_1(verlaine_1_out_7),
    .out_13(jean_paul_sat_1_out_13));
  DotMatrix #(.inputtype("row"), .matrixcols(10), .matrixrows(20)) dotmatrix_1 (
    .row0(jean_paul_sat_1_out_6), .row1(jean_paul_sat_1_out_7), .row2(jean_paul_sat_1_out_8),
    .row3(jean_paul_sat_1_out_9), .row4(jean_paul_sat_1_out_10), .row5(jean_paul_sat_1_out_11),
    .row6(jean_paul_sat_1_out_12), .row7(jean_paul_sat_1_out_14), .row8(jean_paul_sat_1_out_15),
    .row9(jean_paul_sat_1_out_16), .row10(jean_paul_sat_1_out_17), .row11(jean_paul_sat_1_out_18),
    .row12(jean_paul_sat_1_out_19), .row13(jean_paul_sat_1_out_20), .row14(jean_paul_sat_1_out_21),
    .row15(jean_paul_sat_1_out_22), .row16(jean_paul_sat_1_out_23), .row17(jean_paul_sat_1_out_24),
    .row18(jean_paul_sat_1_out_25), .row19(jean_paul_sat_1_out_26));
  Hex_Digit_Display hex_digit_display_2 (.value(verlaine_1_out_4));  // open: dp
  Hex_Digit_Display hex_digit_display_3 (.value(verlaine_1_out_5));  // open: dp
  Button button_1 (.out(button_1_out));
  Button button_2 (.out(button_2_out));
  Button button_3 (.out(button_3_out));
  Button button_4 (.out(button_4_out));
  Hex_Digit_Display hex_digit_display_4 (.value(verlaine_1_out_6));  // open: dp
  Button Start (.out(Start_out));

  // Notes on the sheet:
  //   1 - Setup
  //   Manuel d'utilisation:
  //   Vérifier que: Simulate->Simulation enable est coché
  //   Dans Simulate->Tick Frequency choisissez:
  //   4Hz pour le mode Facile
  //   8Hz pour le mode Normal
  //   16Hz pour le mode Difficile
  //   Appuyer sur crtl+K pour lancer la simulation !
  //   2 - Lancer une partie
  //   Vous pouvez appuyer sur ctrl + R pour reset le jeu
  //   Selectionner la petite main en haut à droite de la fenêtre
  //   Jouez ! Un Flag vous attend si vous atteignez 9999 points !
  //   Maintenant le bouton Start jusqu'à ce que le premier Tetromino apparaissent sur l'écran
endmodule

module Jean_Paul_SAT (
  input  in_1,
  input  in_2,
  input  in_3,
  input  in_4,
  input  in_5,
  output [9:0] out_6,
  output [9:0] out_7,
  output [9:0] out_8,
  output [9:0] out_9,
  output [9:0] out_10,
  output [9:0] out_11,
  output [9:0] out_12,
  output [15:0] out_13,
  output [9:0] out_14,
  output [9:0] out_15,
  output [9:0] out_16,
  output [9:0] out_17,
  output [9:0] out_18,
  output [9:0] out_19,
  output [9:0] out_20,
  output [9:0] out_21,
  output [9:0] out_22,
  output [9:0] out_23,
  output [9:0] out_24,
  output [9:0] out_25,
  output [9:0] out_26
);

  wire and_1_out, and_2_out, and_3_out, baudelaire_1_out_26, baudelaire_1_out_56, clock_1_out,
       corneille_1_out_3, corneille_1_out_4, flaubert_1_out_5, flaubert_1_out_6, or_1_out, or_2_out,
       pagnol_1_out_11, pagnol_1_out_12, pagnol_1_out_13, pagnol_1_out_14, pagnol_1_out_15, pagnol_1_out_16,
       volataire_1_out_3, zola_1_out_11, zola_1_out_12, zola_1_out_13, zola_1_out_14, zola_1_out_15,
       zola_1_out_16, zola_1_out_17;
  wire [1:0] proust_1_out_14;
  wire [2:0] zola_1_out_10;
  wire [3:0] de_beauvoir_1_out_3, de_beauvoir_1_out_4, de_beauvoir_1_out_5, de_beauvoir_1_out_6,
       proust_1_out_15;
  wire [4:0] baudelaire_1_out_57, proust_1_out_13;
  wire [9:0] _1, _2, _3, _4, baudelaire_1_out_27, baudelaire_1_out_28, baudelaire_1_out_29,
       baudelaire_1_out_30, baudelaire_1_out_31, baudelaire_1_out_32, baudelaire_1_out_33,
       baudelaire_1_out_34, baudelaire_1_out_35, baudelaire_1_out_36, baudelaire_1_out_37,
       baudelaire_1_out_38, baudelaire_1_out_39, baudelaire_1_out_40, baudelaire_1_out_41,
       baudelaire_1_out_42, baudelaire_1_out_43, baudelaire_1_out_44, baudelaire_1_out_45,
       baudelaire_1_out_46, baudelaire_1_out_47, baudelaire_1_out_48, baudelaire_1_out_49,
       baudelaire_1_out_50, baudelaire_1_out_51, baudelaire_1_out_52, baudelaire_1_out_53,
       baudelaire_1_out_54, baudelaire_1_out_55, rimbaud_1_out_31, rimbaud_1_out_32, rimbaud_1_out_33,
       rimbaud_1_out_34, rimbaud_1_out_35, rimbaud_1_out_36, rimbaud_1_out_37, rimbaud_1_out_38,
       rimbaud_1_out_39, rimbaud_1_out_40, rimbaud_1_out_41, rimbaud_1_out_42, rimbaud_1_out_43,
       rimbaud_1_out_44, rimbaud_1_out_45, rimbaud_1_out_46, rimbaud_1_out_47, rimbaud_1_out_48,
       rimbaud_1_out_49, rimbaud_1_out_50, rimbaud_1_out_51, rimbaud_1_out_52, rimbaud_1_out_53,
       rimbaud_1_out_54, victor_hugo_1_out_6, victor_hugo_1_out_7, victor_hugo_1_out_8, victor_hugo_1_out_9;
  wire [15:0] counter_1_q, rimbaud_1_out_30, xor_1_out;

  or or_1 (or_1_out, zola_1_out_11, pagnol_1_out_11);
  Rimbaud rimbaud_1 (
    .in_1(baudelaire_1_out_56), .in_3(baudelaire_1_out_57), .in_4(corneille_1_out_4), .in_5(or_1_out),
    .in_6(_1), .in_7(_2), .in_8(_3), .in_9(_4), .in_10(out_6), .in_11(out_7), .in_12(out_8), .in_13(out_9),
    .in_14(out_10), .in_15(out_11), .in_16(out_12), .in_17(out_14), .in_18(out_15), .in_19(out_16),
    .in_20(out_17), .in_21(out_18), .in_22(out_19), .in_23(out_20), .in_24(out_21), .in_25(out_22),
    .in_26(out_23), .in_27(out_24), .in_28(out_25), .in_29(out_26), .out_31(rimbaud_1_out_31),
    .out_32(rimbaud_1_out_32), .out_33(rimbaud_1_out_33), .out_34(rimbaud_1_out_34),
    .out_35(rimbaud_1_out_35), .out_36(rimbaud_1_out_36), .out_37(rimbaud_1_out_37),
    .out_38(rimbaud_1_out_38), .out_39(rimbaud_1_out_39), .out_40(rimbaud_1_out_40),
    .out_41(rimbaud_1_out_41), .out_42(rimbaud_1_out_42), .out_43(rimbaud_1_out_43),
    .out_44(rimbaud_1_out_44), .out_45(rimbaud_1_out_45), .out_46(rimbaud_1_out_46),
    .out_47(rimbaud_1_out_47), .out_48(rimbaud_1_out_48), .out_49(rimbaud_1_out_49),
    .out_50(rimbaud_1_out_50), .out_51(rimbaud_1_out_51), .out_52(rimbaud_1_out_52),
    .out_53(rimbaud_1_out_53), .out_54(rimbaud_1_out_54), .in_2(zola_1_out_12), .out_30(rimbaud_1_out_30));
  De_Beauvoir de_beauvoir_1 (
    .in_1(zola_1_out_10), .in_2(proust_1_out_14), .out_3(de_beauvoir_1_out_3), .out_4(de_beauvoir_1_out_4),
    .out_5(de_beauvoir_1_out_5), .out_6(de_beauvoir_1_out_6));
  Victor_Hugo victor_hugo_1 (
    .in_5(proust_1_out_15), .in_1(de_beauvoir_1_out_3), .in_2(de_beauvoir_1_out_4),
    .in_3(de_beauvoir_1_out_5), .in_4(de_beauvoir_1_out_6), .out_6(victor_hugo_1_out_6),
    .out_7(victor_hugo_1_out_7), .out_8(victor_hugo_1_out_8), .out_9(victor_hugo_1_out_9));
  Baudelaire baudelaire_1 (
    .in_1(rimbaud_1_out_31), .in_2(rimbaud_1_out_32), .in_3(rimbaud_1_out_33), .in_4(rimbaud_1_out_34),
    .in_5(rimbaud_1_out_35), .in_6(rimbaud_1_out_36), .in_7(rimbaud_1_out_37), .in_8(rimbaud_1_out_38),
    .in_9(rimbaud_1_out_39), .in_10(rimbaud_1_out_40), .in_11(rimbaud_1_out_41), .in_12(rimbaud_1_out_42),
    .in_13(rimbaud_1_out_43), .in_14(rimbaud_1_out_44), .in_15(rimbaud_1_out_45), .in_16(rimbaud_1_out_46),
    .in_17(rimbaud_1_out_47), .in_18(rimbaud_1_out_48), .in_19(rimbaud_1_out_49), .in_20(rimbaud_1_out_50),
    .in_21(rimbaud_1_out_51), .in_22(rimbaud_1_out_52), .in_23(rimbaud_1_out_53), .in_24(rimbaud_1_out_54),
    .out_27(baudelaire_1_out_27), .out_28(baudelaire_1_out_28), .out_29(baudelaire_1_out_29),
    .out_30(baudelaire_1_out_30), .out_31(baudelaire_1_out_31), .out_32(baudelaire_1_out_32),
    .out_33(baudelaire_1_out_33), .out_34(baudelaire_1_out_34), .out_35(baudelaire_1_out_35),
    .out_36(baudelaire_1_out_36), .out_37(baudelaire_1_out_37), .out_38(baudelaire_1_out_38),
    .out_39(baudelaire_1_out_39), .out_40(baudelaire_1_out_40), .out_41(baudelaire_1_out_41),
    .out_42(baudelaire_1_out_42), .out_43(baudelaire_1_out_43), .out_44(baudelaire_1_out_44),
    .out_45(baudelaire_1_out_45), .out_46(baudelaire_1_out_46), .out_47(baudelaire_1_out_47),
    .out_48(baudelaire_1_out_48), .out_49(baudelaire_1_out_49), .out_50(baudelaire_1_out_50),
    .in_25(proust_1_out_13), .out_57(baudelaire_1_out_57), .out_51(baudelaire_1_out_51),
    .out_52(baudelaire_1_out_52), .out_53(baudelaire_1_out_53), .out_54(baudelaire_1_out_54),
    .out_55(baudelaire_1_out_55), .out_56(baudelaire_1_out_56), .out_26(baudelaire_1_out_26));
  \Molière  \molière_1  (
    .in_1(baudelaire_1_out_27), .in_2(baudelaire_1_out_28), .in_3(baudelaire_1_out_29),
    .in_4(baudelaire_1_out_30), .in_5(baudelaire_1_out_31), .in_6(baudelaire_1_out_32),
    .in_7(baudelaire_1_out_33), .in_8(baudelaire_1_out_34), .in_9(baudelaire_1_out_35),
    .in_10(baudelaire_1_out_36), .in_12(baudelaire_1_out_37), .in_13(baudelaire_1_out_38),
    .in_14(baudelaire_1_out_39), .in_15(baudelaire_1_out_40), .in_16(baudelaire_1_out_41),
    .in_17(baudelaire_1_out_42), .in_18(baudelaire_1_out_43), .in_19(baudelaire_1_out_44),
    .in_20(baudelaire_1_out_45), .in_21(baudelaire_1_out_46), .in_22(baudelaire_1_out_47),
    .in_24(baudelaire_1_out_48), .in_26(baudelaire_1_out_49), .in_28(baudelaire_1_out_50), .out_38(out_10),
    .out_39(out_11), .out_40(out_12), .out_42(out_15), .out_43(out_16), .out_44(out_17), .out_45(out_18),
    .out_41(out_14), .out_30(_1), .out_31(_2), .out_32(_3), .out_33(_4), .out_34(out_6), .out_35(out_7),
    .out_36(out_8), .out_37(out_9), .out_46(out_19), .out_47(out_20), .out_48(out_21), .out_49(out_22),
    .out_50(out_23), .out_51(out_24), .out_52(out_25), .out_53(out_26), .in_29(victor_hugo_1_out_6),
    .in_27(victor_hugo_1_out_7), .in_25(victor_hugo_1_out_8), .in_23(victor_hugo_1_out_9),
    .in_11(proust_1_out_13));
  Pagnol pagnol_1 (
    .in_5(baudelaire_1_out_55), .in_6(baudelaire_1_out_54), .in_7(baudelaire_1_out_53),
    .in_8(baudelaire_1_out_52), .in_9(baudelaire_1_out_51), .out_11(pagnol_1_out_11),
    .out_12(pagnol_1_out_12), .out_13(pagnol_1_out_13), .in_1(victor_hugo_1_out_6), .in_10(proust_1_out_15),
    .in_2(victor_hugo_1_out_7), .in_3(victor_hugo_1_out_8), .in_4(victor_hugo_1_out_9),
    .out_14(pagnol_1_out_14), .out_15(pagnol_1_out_15), .out_16(pagnol_1_out_16));
  Zola zola_1 (
    .in_6(in_2), .in_7(in_3), .in_8(in_4), .in_9(in_5), .out_15(zola_1_out_15), .out_16(zola_1_out_16),
    .out_17(zola_1_out_17), .in_4(and_2_out), .out_10(zola_1_out_10), .in_1(corneille_1_out_4),
    .in_2(and_1_out), .out_11(zola_1_out_11), .out_12(zola_1_out_12), .out_14(zola_1_out_14),
    .Key(xor_1_out), .patterne(out_13), .out_13(zola_1_out_13));
  Proust proust_1 (
    .in_3(pagnol_1_out_15), .in_4(pagnol_1_out_14), .in_6(pagnol_1_out_11), .in_8(and_1_out),
    .in_11(pagnol_1_out_12), .in_12(pagnol_1_out_13), .out_14(proust_1_out_14), .out_13(proust_1_out_13),
    .out_15(proust_1_out_15), .in_1(zola_1_out_13), .in_9(zola_1_out_17), .in_2(zola_1_out_15),
    .in_10(zola_1_out_16), .in_5(corneille_1_out_4), .in_7(zola_1_out_14));
  and and_1 (and_1_out, corneille_1_out_4, or_2_out);
  and and_2 (and_2_out, ~baudelaire_1_out_26, ~volataire_1_out_3, flaubert_1_out_6);  // AND_Gate
  assign xor_1_out = rimbaud_1_out_30 ^ counter_1_q;  // XOR_Gate xor_1, 16 bits wide
  and and_3 (and_3_out, baudelaire_1_out_56, ~corneille_1_out_4);  // AND_Gate
  or or_2 (or_2_out, pagnol_1_out_16, corneille_1_out_3);
  Counter #(.width(16), .max('hffff)) counter_1 (.Q(counter_1_q), .clk(and_3_out));  // open: load, D, count, carry, clr
  Volataire volataire_1 (.in_1(flaubert_1_out_5), .in_2(counter_1_q), .out_3(volataire_1_out_3));
  Flaubert flaubert_1 (
    .in_1(baudelaire_1_out_56), .in_2(corneille_1_out_4), .in_3(corneille_1_out_3), .out_5(flaubert_1_out_5),
    .out_4(out_13), .out_6(flaubert_1_out_6));
  Corneille corneille_1 (.in_2(clock_1_out), .out_3(corneille_1_out_3), .in_1(in_1), .out_4(corneille_1_out_4));
  Clock clock_1 (.out(clock_1_out));

  // Other names for the same wires on the sheet: _5[9:0] = out_6; _6[9:0] = out_7; _7[9:0] = out_8; _8[9:0] = out_9;
  //   _9[9:0] = out_10; _10[9:0] = out_11; _11[9:0] = out_12; _12[9:0] = out_14; _13[9:0] = out_15; _14[9:0] = out_16;
  //   _15[9:0] = out_17; _16[9:0] = out_18; _17[9:0] = out_19; _18[9:0] = out_20; _19[9:0] = out_21;
  //   _20[9:0] = out_22; _21[9:0] = out_23; _22[9:0] = out_24; _23[9:0] = out_25; _24[9:0] = out_26
endmodule

module \Molière  (
  input  [9:0] in_1,
  input  [9:0] in_2,
  input  [9:0] in_3,
  input  [9:0] in_4,
  input  [9:0] in_5,
  input  [9:0] in_6,
  input  [9:0] in_7,
  input  [9:0] in_8,
  input  [9:0] in_9,
  input  [9:0] in_10,
  input  [4:0] in_11,
  input  [9:0] in_12,
  input  [9:0] in_13,
  input  [9:0] in_14,
  input  [9:0] in_15,
  input  [9:0] in_16,
  input  [9:0] in_17,
  input  [9:0] in_18,
  input  [9:0] in_19,
  input  [9:0] in_20,
  input  [9:0] in_21,
  input  [9:0] in_22,
  input  [9:0] in_23,
  input  [9:0] in_24,
  input  [9:0] in_25,
  input  [9:0] in_26,
  input  [9:0] in_27,
  input  [9:0] in_28,
  input  [9:0] in_29,
  output [9:0] out_30,
  output [9:0] out_31,
  output [9:0] out_32,
  output [9:0] out_33,
  output [9:0] out_34,
  output [9:0] out_35,
  output [9:0] out_36,
  output [9:0] out_37,
  output [9:0] out_38,
  output [9:0] out_39,
  output [9:0] out_40,
  output [9:0] out_41,
  output [9:0] out_42,
  output [9:0] out_43,
  output [9:0] out_44,
  output [9:0] out_45,
  output [9:0] out_46,
  output [9:0] out_47,
  output [9:0] out_48,
  output [9:0] out_49,
  output [9:0] out_50,
  output [9:0] out_51,
  output [9:0] out_52,
  output [9:0] out_53
);

  wire [4:0] adder_1_out, subtractor_1_out, subtractor_2_out;
  wire [9:0] d_artagnan_1_out_27, d_artagnan_1_out_28, d_artagnan_1_out_29, d_artagnan_1_out_30,
       d_artagnan_1_out_31, d_artagnan_1_out_32, d_artagnan_1_out_33, d_artagnan_1_out_34,
       d_artagnan_1_out_35, d_artagnan_1_out_36, d_artagnan_1_out_37, d_artagnan_1_out_38,
       d_artagnan_1_out_39, d_artagnan_1_out_40, d_artagnan_1_out_41, d_artagnan_1_out_42,
       d_artagnan_1_out_43, d_artagnan_1_out_44, d_artagnan_1_out_45, d_artagnan_1_out_46,
       d_artagnan_1_out_47, d_artagnan_1_out_48, d_artagnan_1_out_49, d_artagnan_1_out_50,
       d_artagnan_2_out_27, d_artagnan_2_out_28, d_artagnan_2_out_29, d_artagnan_2_out_30,
       d_artagnan_2_out_31, d_artagnan_2_out_32, d_artagnan_2_out_33, d_artagnan_2_out_34,
       d_artagnan_2_out_35, d_artagnan_2_out_36, d_artagnan_2_out_37, d_artagnan_2_out_38,
       d_artagnan_2_out_39, d_artagnan_2_out_40, d_artagnan_2_out_41, d_artagnan_2_out_42,
       d_artagnan_2_out_43, d_artagnan_2_out_44, d_artagnan_2_out_45, d_artagnan_2_out_46,
       d_artagnan_2_out_47, d_artagnan_2_out_48, d_artagnan_2_out_49, d_artagnan_2_out_50,
       d_artagnan_3_out_27, d_artagnan_3_out_28, d_artagnan_3_out_29, d_artagnan_3_out_30,
       d_artagnan_3_out_31, d_artagnan_3_out_32, d_artagnan_3_out_33, d_artagnan_3_out_34,
       d_artagnan_3_out_35, d_artagnan_3_out_36, d_artagnan_3_out_37, d_artagnan_3_out_38,
       d_artagnan_3_out_39, d_artagnan_3_out_40, d_artagnan_3_out_41, d_artagnan_3_out_42,
       d_artagnan_3_out_43, d_artagnan_3_out_44, d_artagnan_3_out_45, d_artagnan_3_out_46,
       d_artagnan_3_out_47, d_artagnan_3_out_48, d_artagnan_3_out_49, d_artagnan_3_out_50,
       d_artagnan_4_out_27, d_artagnan_4_out_28, d_artagnan_4_out_29, d_artagnan_4_out_30,
       d_artagnan_4_out_31, d_artagnan_4_out_32, d_artagnan_4_out_33, d_artagnan_4_out_34,
       d_artagnan_4_out_35, d_artagnan_4_out_36, d_artagnan_4_out_37, d_artagnan_4_out_38,
       d_artagnan_4_out_39, d_artagnan_4_out_40, d_artagnan_4_out_41, d_artagnan_4_out_42,
       d_artagnan_4_out_43, d_artagnan_4_out_44, d_artagnan_4_out_45, d_artagnan_4_out_46,
       d_artagnan_4_out_47, d_artagnan_4_out_48, d_artagnan_4_out_49, d_artagnan_4_out_50;

  Subtractor #(.width(5)) subtractor_1 (
    .a(subtractor_2_out), .b({5{1'b0}}), .out(subtractor_1_out), .bin(1'b1));  // open: bout
  Subtractor #(.width(5)) subtractor_2 (.a(in_11), .b({5{1'b0}}), .out(subtractor_2_out), .bin(1'b1));  // open: bout
  Adder #(.width(5)) adder_1 (.a(in_11), .b({5{1'b0}}), .out(adder_1_out), .cin(1'b1));  // open: cout
  D_Artagnan d_artagnan_1 (
    .in_3(in_1), .in_4(in_2), .in_5(in_3), .in_6(in_4), .in_7(in_5), .in_8(in_6), .in_9(in_7), .in_10(in_8),
    .in_11(in_9), .in_12(in_10), .in_13(in_12), .in_14(in_13), .in_15(in_14), .in_16(in_15), .in_17(in_16),
    .in_18(in_17), .in_19(in_18), .in_20(in_19), .in_21(in_20), .in_22(in_21), .in_23(in_22), .in_24(in_24),
    .in_25(in_26), .in_26(in_28), .in_1(subtractor_1_out), .in_2(in_23), .out_27(d_artagnan_1_out_27),
    .out_28(d_artagnan_1_out_28), .out_29(d_artagnan_1_out_29), .out_30(d_artagnan_1_out_30),
    .out_31(d_artagnan_1_out_31), .out_32(d_artagnan_1_out_32), .out_33(d_artagnan_1_out_33),
    .out_34(d_artagnan_1_out_34), .out_35(d_artagnan_1_out_35), .out_36(d_artagnan_1_out_36),
    .out_37(d_artagnan_1_out_37), .out_38(d_artagnan_1_out_38), .out_39(d_artagnan_1_out_39),
    .out_40(d_artagnan_1_out_40), .out_41(d_artagnan_1_out_41), .out_42(d_artagnan_1_out_42),
    .out_43(d_artagnan_1_out_43), .out_44(d_artagnan_1_out_44), .out_45(d_artagnan_1_out_45),
    .out_46(d_artagnan_1_out_46), .out_47(d_artagnan_1_out_47), .out_48(d_artagnan_1_out_48),
    .out_49(d_artagnan_1_out_49), .out_50(d_artagnan_1_out_50));
  D_Artagnan d_artagnan_2 (
    .in_3(in_1), .in_4(in_2), .in_5(in_3), .in_6(in_4), .in_7(in_5), .in_8(in_6), .in_9(in_7), .in_10(in_8),
    .in_11(in_9), .in_12(in_10), .in_13(in_12), .in_14(in_13), .in_15(in_14), .in_16(in_15), .in_17(in_16),
    .in_18(in_17), .in_19(in_18), .in_20(in_19), .in_21(in_20), .in_22(in_21), .in_23(in_22), .in_24(in_24),
    .in_25(in_26), .in_26(in_28), .in_1(subtractor_2_out), .in_2(in_25), .out_27(d_artagnan_2_out_27),
    .out_28(d_artagnan_2_out_28), .out_29(d_artagnan_2_out_29), .out_30(d_artagnan_2_out_30),
    .out_31(d_artagnan_2_out_31), .out_32(d_artagnan_2_out_32), .out_33(d_artagnan_2_out_33),
    .out_34(d_artagnan_2_out_34), .out_35(d_artagnan_2_out_35), .out_36(d_artagnan_2_out_36),
    .out_37(d_artagnan_2_out_37), .out_38(d_artagnan_2_out_38), .out_39(d_artagnan_2_out_39),
    .out_40(d_artagnan_2_out_40), .out_41(d_artagnan_2_out_41), .out_42(d_artagnan_2_out_42),
    .out_43(d_artagnan_2_out_43), .out_44(d_artagnan_2_out_44), .out_45(d_artagnan_2_out_45),
    .out_46(d_artagnan_2_out_46), .out_47(d_artagnan_2_out_47), .out_48(d_artagnan_2_out_48),
    .out_49(d_artagnan_2_out_49), .out_50(d_artagnan_2_out_50));
  D_Artagnan d_artagnan_3 (
    .in_3(in_1), .in_4(in_2), .in_5(in_3), .in_6(in_4), .in_7(in_5), .in_8(in_6), .in_9(in_7), .in_10(in_8),
    .in_11(in_9), .in_12(in_10), .in_13(in_12), .in_14(in_13), .in_15(in_14), .in_16(in_15), .in_17(in_16),
    .in_18(in_17), .in_19(in_18), .in_20(in_19), .in_21(in_20), .in_22(in_21), .in_23(in_22), .in_24(in_24),
    .in_25(in_26), .in_26(in_28), .in_1(in_11), .in_2(in_27), .out_27(d_artagnan_3_out_27),
    .out_28(d_artagnan_3_out_28), .out_29(d_artagnan_3_out_29), .out_30(d_artagnan_3_out_30),
    .out_31(d_artagnan_3_out_31), .out_32(d_artagnan_3_out_32), .out_33(d_artagnan_3_out_33),
    .out_34(d_artagnan_3_out_34), .out_35(d_artagnan_3_out_35), .out_36(d_artagnan_3_out_36),
    .out_37(d_artagnan_3_out_37), .out_38(d_artagnan_3_out_38), .out_39(d_artagnan_3_out_39),
    .out_40(d_artagnan_3_out_40), .out_41(d_artagnan_3_out_41), .out_42(d_artagnan_3_out_42),
    .out_43(d_artagnan_3_out_43), .out_44(d_artagnan_3_out_44), .out_45(d_artagnan_3_out_45),
    .out_46(d_artagnan_3_out_46), .out_47(d_artagnan_3_out_47), .out_48(d_artagnan_3_out_48),
    .out_49(d_artagnan_3_out_49), .out_50(d_artagnan_3_out_50));
  D_Artagnan d_artagnan_4 (
    .in_3(in_1), .in_4(in_2), .in_5(in_3), .in_6(in_4), .in_7(in_5), .in_8(in_6), .in_9(in_7), .in_10(in_8),
    .in_11(in_9), .in_12(in_10), .in_13(in_12), .in_14(in_13), .in_15(in_14), .in_16(in_15), .in_17(in_16),
    .in_18(in_17), .in_19(in_18), .in_20(in_19), .in_21(in_20), .in_22(in_21), .in_23(in_22), .in_24(in_24),
    .in_25(in_26), .in_26(in_28), .in_1(adder_1_out), .in_2(in_29), .out_27(d_artagnan_4_out_27),
    .out_28(d_artagnan_4_out_28), .out_29(d_artagnan_4_out_29), .out_30(d_artagnan_4_out_30),
    .out_31(d_artagnan_4_out_31), .out_32(d_artagnan_4_out_32), .out_33(d_artagnan_4_out_33),
    .out_34(d_artagnan_4_out_34), .out_35(d_artagnan_4_out_35), .out_36(d_artagnan_4_out_36),
    .out_37(d_artagnan_4_out_37), .out_38(d_artagnan_4_out_38), .out_39(d_artagnan_4_out_39),
    .out_40(d_artagnan_4_out_40), .out_41(d_artagnan_4_out_41), .out_42(d_artagnan_4_out_42),
    .out_43(d_artagnan_4_out_43), .out_44(d_artagnan_4_out_44), .out_45(d_artagnan_4_out_45),
    .out_46(d_artagnan_4_out_46), .out_47(d_artagnan_4_out_47), .out_48(d_artagnan_4_out_48),
    .out_49(d_artagnan_4_out_49), .out_50(d_artagnan_4_out_50));
  assign out_30 = d_artagnan_1_out_27 | d_artagnan_2_out_27 | d_artagnan_3_out_27 | d_artagnan_4_out_27;  // OR_Gate or_1, 10 bits wide
  assign out_31 = d_artagnan_1_out_28 | d_artagnan_2_out_28 | d_artagnan_3_out_28 | d_artagnan_4_out_28;  // OR_Gate or_2, 10 bits wide
  assign out_32 = d_artagnan_1_out_29 | d_artagnan_2_out_29 | d_artagnan_3_out_29 | d_artagnan_4_out_29;  // OR_Gate or_3, 10 bits wide
  assign out_33 = d_artagnan_1_out_30 | d_artagnan_2_out_30 | d_artagnan_3_out_30 | d_artagnan_4_out_30;  // OR_Gate or_4, 10 bits wide
  assign out_34 = d_artagnan_1_out_31 | d_artagnan_2_out_31 | d_artagnan_3_out_31 | d_artagnan_4_out_31;  // OR_Gate or_5, 10 bits wide
  assign out_36 = d_artagnan_1_out_33 | d_artagnan_2_out_33 | d_artagnan_3_out_33 | d_artagnan_4_out_33;  // OR_Gate or_6, 10 bits wide
  assign out_35 = d_artagnan_1_out_32 | d_artagnan_2_out_32 | d_artagnan_3_out_32 | d_artagnan_4_out_32;  // OR_Gate or_7, 10 bits wide
  assign out_38 = d_artagnan_1_out_35 | d_artagnan_2_out_35 | d_artagnan_3_out_35 | d_artagnan_4_out_35;  // OR_Gate or_8, 10 bits wide
  assign out_37 = d_artagnan_1_out_34 | d_artagnan_2_out_34 | d_artagnan_3_out_34 | d_artagnan_4_out_34;  // OR_Gate or_9, 10 bits wide
  assign out_39 = d_artagnan_1_out_36 | d_artagnan_2_out_36 | d_artagnan_3_out_36 | d_artagnan_4_out_36;  // OR_Gate or_10, 10 bits wide
  assign out_41 = d_artagnan_1_out_38 | d_artagnan_2_out_38 | d_artagnan_3_out_38 | d_artagnan_4_out_38;  // OR_Gate or_11, 10 bits wide
  assign out_40 = d_artagnan_1_out_37 | d_artagnan_2_out_37 | d_artagnan_3_out_37 | d_artagnan_4_out_37;  // OR_Gate or_12, 10 bits wide
  assign out_42 = d_artagnan_1_out_39 | d_artagnan_2_out_39 | d_artagnan_3_out_39 | d_artagnan_4_out_39;  // OR_Gate or_13, 10 bits wide
  assign out_43 = d_artagnan_1_out_40 | d_artagnan_2_out_40 | d_artagnan_3_out_40 | d_artagnan_4_out_40;  // OR_Gate or_14, 10 bits wide
  assign out_44 = d_artagnan_1_out_41 | d_artagnan_2_out_41 | d_artagnan_3_out_41 | d_artagnan_4_out_41;  // OR_Gate or_15, 10 bits wide
  assign out_46 = d_artagnan_1_out_43 | d_artagnan_2_out_43 | d_artagnan_3_out_43 | d_artagnan_4_out_43;  // OR_Gate or_16, 10 bits wide
  assign out_45 = d_artagnan_1_out_42 | d_artagnan_2_out_42 | d_artagnan_3_out_42 | d_artagnan_4_out_42;  // OR_Gate or_17, 10 bits wide
  assign out_47 = d_artagnan_1_out_44 | d_artagnan_2_out_44 | d_artagnan_3_out_44 | d_artagnan_4_out_44;  // OR_Gate or_18, 10 bits wide
  assign out_49 = d_artagnan_1_out_46 | d_artagnan_2_out_46 | d_artagnan_3_out_46 | d_artagnan_4_out_46;  // OR_Gate or_19, 10 bits wide
  assign out_48 = d_artagnan_1_out_45 | d_artagnan_2_out_45 | d_artagnan_3_out_45 | d_artagnan_4_out_45;  // OR_Gate or_20, 10 bits wide
  assign out_50 = d_artagnan_1_out_47 | d_artagnan_2_out_47 | d_artagnan_3_out_47 | d_artagnan_4_out_47;  // OR_Gate or_21, 10 bits wide
  assign out_51 = d_artagnan_1_out_48 | d_artagnan_2_out_48 | d_artagnan_3_out_48 | d_artagnan_4_out_48;  // OR_Gate or_22, 10 bits wide
  assign out_52 = d_artagnan_1_out_49 | d_artagnan_2_out_49 | d_artagnan_3_out_49 | d_artagnan_4_out_49;  // OR_Gate or_23, 10 bits wide
  assign out_53 = d_artagnan_1_out_50 | d_artagnan_2_out_50 | d_artagnan_3_out_50 | d_artagnan_4_out_50;  // OR_Gate or_24, 10 bits wide
endmodule

module Rimbaud (
  input  in_1,
  input  in_2,
  input  [4:0] in_3,
  input  in_4,
  input  in_5,
  input  [9:0] in_6,
  input  [9:0] in_7,
  input  [9:0] in_8,
  input  [9:0] in_9,
  input  [9:0] in_10,
  input  [9:0] in_11,
  input  [9:0] in_12,
  input  [9:0] in_13,
  input  [9:0] in_14,
  input  [9:0] in_15,
  input  [9:0] in_16,
  input  [9:0] in_17,
  input  [9:0] in_18,
  input  [9:0] in_19,
  input  [9:0] in_20,
  input  [9:0] in_21,
  input  [9:0] in_22,
  input  [9:0] in_23,
  input  [9:0] in_24,
  input  [9:0] in_25,
  input  [9:0] in_26,
  input  [9:0] in_27,
  input  [9:0] in_28,
  input  [9:0] in_29,
  output [15:0] out_30,
  output [9:0] out_31,
  output [9:0] out_32,
  output [9:0] out_33,
  output [9:0] out_34,
  output [9:0] out_35,
  output [9:0] out_36,
  output [9:0] out_37,
  output [9:0] out_38,
  output [9:0] out_39,
  output [9:0] out_40,
  output [9:0] out_41,
  output [9:0] out_42,
  output [9:0] out_43,
  output [9:0] out_44,
  output [9:0] out_45,
  output [9:0] out_46,
  output [9:0] out_47,
  output [9:0] out_48,
  output [9:0] out_49,
  output [9:0] out_50,
  output [9:0] out_51,
  output [9:0] out_52,
  output [9:0] out_53,
  output [9:0] out_54
);

  wire and_1_out, multiplexer_1_out, rousseaux_1__0, rousseaux_1__1, rousseaux_1__2, rousseaux_1__3,
       rousseaux_1__4, rousseaux_1__5, rousseaux_1__6, rousseaux_1__7, rousseaux_1__8, rousseaux_1__9,
       rousseaux_1__10, rousseaux_1__11, rousseaux_1__12, rousseaux_1__13, rousseaux_1__14, rousseaux_1__15,
       rousseaux_1__16, rousseaux_1__17, rousseaux_1__18, rousseaux_1__19, rousseaux_1__20, rousseaux_1__21,
       rousseaux_1__22, rousseaux_1__23;
  wire [4:0] multiplexer_2_out;
  wire [9:0] controlled_buffer_1_out, controlled_buffer_3_out, controlled_buffer_5_out,
       controlled_buffer_7_out, controlled_buffer_9_out, controlled_buffer_11_out, controlled_buffer_13_out,
       controlled_buffer_15_out, controlled_buffer_17_out, controlled_buffer_19_out,
       controlled_buffer_21_out, controlled_buffer_23_out, controlled_buffer_25_out,
       controlled_buffer_27_out, controlled_buffer_29_out, controlled_buffer_31_out,
       controlled_buffer_33_out, controlled_buffer_35_out, controlled_buffer_37_out,
       controlled_buffer_39_out, controlled_buffer_41_out, controlled_buffer_43_out,
       controlled_buffer_45_out, controlled_buffer_47_out;

  Multiplexer #(.disabled(0), .enable("false")) multiplexer_1 (
    .in0(in_1), .in1(1'b1), .out(multiplexer_1_out), .sel(in_2));
  Multiplexer #(.width(5), .disabled(0), .enable("false")) multiplexer_2 (
    .in0(in_3), .in1({5{1'b1}}), .out(multiplexer_2_out), .sel(in_2));
  Rousseaux rousseaux_1 (
    .in_1(multiplexer_1_out), .in_2(multiplexer_2_out), ._0(rousseaux_1__0), ._1(rousseaux_1__1),
    ._2(rousseaux_1__2), ._3(rousseaux_1__3), ._4(rousseaux_1__4), ._5(rousseaux_1__5), ._6(rousseaux_1__6),
    ._7(rousseaux_1__7), ._8(rousseaux_1__8), ._9(rousseaux_1__9), ._10(rousseaux_1__10),
    ._11(rousseaux_1__11), ._12(rousseaux_1__12), ._13(rousseaux_1__13), ._14(rousseaux_1__14),
    ._15(rousseaux_1__15), ._16(rousseaux_1__16), ._17(rousseaux_1__17), ._18(rousseaux_1__18),
    ._19(rousseaux_1__19), ._20(rousseaux_1__20), ._21(rousseaux_1__21), ._22(rousseaux_1__22),
    ._23(rousseaux_1__23));
  assign controlled_buffer_1_out = rousseaux_1__0 ? {10{1'b0}} : 10'bz;  // Controlled_Buffer controlled_buffer_1
  assign controlled_buffer_1_out = in_5 ? in_6 : 10'bz;  // Controlled_Buffer controlled_buffer_2
  assign controlled_buffer_3_out = rousseaux_1__1 ? out_31 : 10'bz;  // Controlled_Buffer controlled_buffer_3
  Register #(.width(10)) register_1 (.D(controlled_buffer_1_out), .Q(out_31), .clk(in_4));  // open: en, clr
  assign controlled_buffer_3_out = in_5 ? in_7 : 10'bz;  // Controlled_Buffer controlled_buffer_4
  assign controlled_buffer_5_out = rousseaux_1__2 ? out_32 : 10'bz;  // Controlled_Buffer controlled_buffer_5
  Register #(.width(10)) register_2 (.D(controlled_buffer_3_out), .Q(out_32), .clk(in_4));  // open: en, clr
  assign controlled_buffer_5_out = in_5 ? in_8 : 10'bz;  // Controlled_Buffer controlled_buffer_6
  assign controlled_buffer_7_out = rousseaux_1__3 ? out_33 : 10'bz;  // Controlled_Buffer controlled_buffer_7
  Register #(.width(10)) register_3 (.D(controlled_buffer_5_out), .Q(out_33), .clk(in_4));  // open: en, clr
  Register #(.width(10)) register_4 (.D(controlled_buffer_7_out), .Q(out_34), .clk(in_4));  // open: en, clr
  assign controlled_buffer_7_out = in_5 ? in_9 : 10'bz;  // Controlled_Buffer controlled_buffer_8
  Register #(.width(10)) register_5 (.D(controlled_buffer_9_out), .Q(out_35), .clk(in_4));  // open: en, clr
  assign controlled_buffer_9_out = rousseaux_1__4 ? out_34 : 10'bz;  // Controlled_Buffer controlled_buffer_9
  assign controlled_buffer_9_out = in_5 ? in_10 : 10'bz;  // Controlled_Buffer controlled_buffer_10
  assign controlled_buffer_11_out = rousseaux_1__5 ? out_35 : 10'bz;  // Controlled_Buffer controlled_buffer_11
  Register #(.width(10)) register_6 (.D(controlled_buffer_11_out), .Q(out_36), .clk(in_4));  // open: en, clr
  assign controlled_buffer_11_out = in_5 ? in_11 : 10'bz;  // Controlled_Buffer controlled_buffer_12
  assign controlled_buffer_13_out = rousseaux_1__6 ? out_36 : 10'bz;  // Controlled_Buffer controlled_buffer_13
  Register #(.width(10)) register_7 (.D(controlled_buffer_13_out), .Q(out_37), .clk(in_4));  // open: en, clr
  assign controlled_buffer_13_out = in_5 ? in_12 : 10'bz;  // Controlled_Buffer controlled_buffer_14
  assign controlled_buffer_15_out = rousseaux_1__7 ? out_37 : 10'bz;  // Controlled_Buffer controlled_buffer_15
  assign controlled_buffer_15_out = in_5 ? in_13 : 10'bz;  // Controlled_Buffer controlled_buffer_16
  assign controlled_buffer_17_out = rousseaux_1__8 ? out_38 : 10'bz;  // Controlled_Buffer controlled_buffer_17
  Register #(.width(10)) register_8 (.D(controlled_buffer_15_out), .Q(out_38), .clk(in_4));  // open: en, clr
  assign controlled_buffer_17_out = in_5 ? in_14 : 10'bz;  // Controlled_Buffer controlled_buffer_18
  Register #(.width(10)) register_9 (.D(controlled_buffer_17_out), .Q(out_39), .clk(in_4));  // open: en, clr
  assign controlled_buffer_19_out = rousseaux_1__9 ? out_39 : 10'bz;  // Controlled_Buffer controlled_buffer_19
  assign controlled_buffer_19_out = in_5 ? in_15 : 10'bz;  // Controlled_Buffer controlled_buffer_20
  Register #(.width(10)) register_10 (.D(controlled_buffer_19_out), .Q(out_40), .clk(in_4));  // open: en, clr
  assign controlled_buffer_21_out = rousseaux_1__10 ? out_40 : 10'bz;  // Controlled_Buffer controlled_buffer_21
  assign controlled_buffer_21_out = in_5 ? in_16 : 10'bz;  // Controlled_Buffer controlled_buffer_22
  assign controlled_buffer_23_out = rousseaux_1__11 ? out_41 : 10'bz;  // Controlled_Buffer controlled_buffer_23
  Register #(.width(10)) register_11 (.D(controlled_buffer_21_out), .Q(out_41), .clk(in_4));  // open: en, clr
  Register #(.width(10)) register_12 (.D(controlled_buffer_23_out), .Q(out_42), .clk(in_4));  // open: en, clr
  assign controlled_buffer_23_out = in_5 ? in_17 : 10'bz;  // Controlled_Buffer controlled_buffer_24
  Register #(.width(10)) register_13 (.D(controlled_buffer_25_out), .Q(out_43), .clk(in_4));  // open: en, clr
  assign controlled_buffer_25_out = rousseaux_1__12 ? out_42 : 10'bz;  // Controlled_Buffer controlled_buffer_25
  assign controlled_buffer_25_out = in_5 ? in_18 : 10'bz;  // Controlled_Buffer controlled_buffer_26
  assign controlled_buffer_27_out = rousseaux_1__13 ? out_43 : 10'bz;  // Controlled_Buffer controlled_buffer_27
  Register #(.width(10)) register_14 (.D(controlled_buffer_27_out), .Q(out_44), .clk(in_4));  // open: en, clr
  assign controlled_buffer_27_out = in_5 ? in_19 : 10'bz;  // Controlled_Buffer controlled_buffer_28
  Register #(.width(10)) register_15 (.D(controlled_buffer_29_out), .Q(out_45), .clk(in_4));  // open: en, clr
  assign controlled_buffer_29_out = rousseaux_1__14 ? out_44 : 10'bz;  // Controlled_Buffer controlled_buffer_29
  assign controlled_buffer_29_out = in_5 ? in_20 : 10'bz;  // Controlled_Buffer controlled_buffer_30
  assign controlled_buffer_31_out = rousseaux_1__15 ? out_45 : 10'bz;  // Controlled_Buffer controlled_buffer_31
  assign controlled_buffer_31_out = in_5 ? in_21 : 10'bz;  // Controlled_Buffer controlled_buffer_32
  assign controlled_buffer_33_out = rousseaux_1__16 ? out_46 : 10'bz;  // Controlled_Buffer controlled_buffer_33
  Register #(.width(10)) register_16 (.D(controlled_buffer_31_out), .Q(out_46), .clk(in_4));  // open: en, clr
  assign controlled_buffer_33_out = in_5 ? in_22 : 10'bz;  // Controlled_Buffer controlled_buffer_34
  assign controlled_buffer_35_out = rousseaux_1__17 ? out_47 : 10'bz;  // Controlled_Buffer controlled_buffer_35
  Register #(.width(10)) register_17 (.D(controlled_buffer_33_out), .Q(out_47), .clk(in_4));  // open: en, clr
  assign controlled_buffer_35_out = in_5 ? in_23 : 10'bz;  // Controlled_Buffer controlled_buffer_36
  assign controlled_buffer_37_out = rousseaux_1__18 ? out_48 : 10'bz;  // Controlled_Buffer controlled_buffer_37
  Register #(.width(10)) register_18 (.D(controlled_buffer_35_out), .Q(out_48), .clk(in_4));  // open: en, clr
  assign controlled_buffer_37_out = in_5 ? in_24 : 10'bz;  // Controlled_Buffer controlled_buffer_38
  Register #(.width(10)) register_19 (.D(controlled_buffer_37_out), .Q(out_49), .clk(in_4));  // open: en, clr
  assign controlled_buffer_39_out = rousseaux_1__19 ? out_49 : 10'bz;  // Controlled_Buffer controlled_buffer_39
  Register #(.width(10)) register_20 (.D(controlled_buffer_39_out), .Q(out_50), .clk(in_4));  // open: en, clr
  assign controlled_buffer_39_out = in_5 ? in_25 : 10'bz;  // Controlled_Buffer controlled_buffer_40
  assign controlled_buffer_41_out = rousseaux_1__20 ? out_50 : 10'bz;  // Controlled_Buffer controlled_buffer_41
  Register #(.width(10)) register_21 (.D(controlled_buffer_41_out), .Q(out_51), .clk(in_4));  // open: en, clr
  assign controlled_buffer_41_out = in_5 ? in_26 : 10'bz;  // Controlled_Buffer controlled_buffer_42
  Register #(.width(10)) register_22 (.D(controlled_buffer_43_out), .Q(out_52), .clk(in_4));  // open: en, clr
  assign controlled_buffer_43_out = rousseaux_1__21 ? out_51 : 10'bz;  // Controlled_Buffer controlled_buffer_43
  assign controlled_buffer_43_out = in_5 ? in_27 : 10'bz;  // Controlled_Buffer controlled_buffer_44
  assign controlled_buffer_45_out = rousseaux_1__22 ? out_52 : 10'bz;  // Controlled_Buffer controlled_buffer_45
  Register #(.width(10)) register_23 (.D(controlled_buffer_45_out), .Q(out_53), .clk(in_4));  // open: en, clr
  assign controlled_buffer_45_out = in_5 ? in_28 : 10'bz;  // Controlled_Buffer controlled_buffer_46
  assign controlled_buffer_47_out = rousseaux_1__23 ? out_53 : 10'bz;  // Controlled_Buffer controlled_buffer_47
  assign controlled_buffer_47_out = in_5 ? in_29 : 10'bz;  // Controlled_Buffer controlled_buffer_48
  and and_1 (and_1_out, in_1, ~in_4);  // AND_Gate
  Register #(.width(10)) register_24 (.D(controlled_buffer_47_out), .Q(out_54), .clk(in_4));  // open: en, clr
  Random #(.width(16), .seed(4040)) random_1 (.clk(and_1_out), .out(out_30));  // open: next, clr
endmodule

module Volataire (
  input  in_1,
  input  [15:0] in_2,
  output out_3
);

  wire d_ff_1_qn, d_ff_2_qn, d_ff_3_qn, d_ff_4_qn, d_ff_5_qn, d_ff_6_qn, d_ff_7_qn, d_ff_8_qn, d_ff_9_qn,
       not_1_out, not_2_out, not_3_out, not_4_out, not_5_out, not_6_out, not_7_out, not_8_out, not_9_out,
       not_10_out, not_11_out, not_12_out, not_13_out, not_14_out, not_15_out, not_16_out;
  wire [8:0] d_ff_9_q, xor_1_out;

  D_Flip_Flop d_ff_1 (.clk(in_1), .D(d_ff_9_qn), .Q(d_ff_9_q[8]), .Qn(d_ff_1_qn));  // open: preset, en, reset
  D_Flip_Flop d_ff_2 (.clk(not_1_out), .D(not_2_out), .Q(d_ff_9_q[7]), .Qn(d_ff_2_qn));  // open: preset, en, reset
  not not_1 (not_1_out, in_1);
  not not_2 (not_2_out, d_ff_1_qn);
  not not_3 (not_3_out, in_1);
  not not_4 (not_4_out, d_ff_2_qn);
  assign xor_1_out = d_ff_9_q ^ {in_2[15], in_2[13], in_2[9:5], in_2[3], in_2[1]};  // XOR_Gate xor_1, 9 bits wide
  D_Flip_Flop d_ff_3 (.clk(not_3_out), .D(not_4_out), .Q(d_ff_9_q[6]), .Qn(d_ff_3_qn));  // open: preset, en, reset
  not not_5 (not_5_out, in_1);
  not not_6 (not_6_out, d_ff_3_qn);
  BitFinder #(.width(9)) bitfinder_1 (.in(xor_1_out), .found(out_3));  // open: index
  D_Flip_Flop d_ff_4 (.clk(not_5_out), .D(not_6_out), .Q(d_ff_9_q[5]), .Qn(d_ff_4_qn));  // open: preset, en, reset
  D_Flip_Flop d_ff_5 (.clk(not_7_out), .D(not_8_out), .Q(d_ff_9_q[4]), .Qn(d_ff_5_qn));  // open: preset, en, reset
  not not_7 (not_7_out, in_1);
  not not_8 (not_8_out, d_ff_4_qn);
  not not_9 (not_9_out, in_1);
  D_Flip_Flop d_ff_6 (.clk(not_9_out), .D(not_10_out), .Q(d_ff_9_q[3]), .Qn(d_ff_6_qn));  // open: preset, en, reset
  not not_10 (not_10_out, d_ff_5_qn);
  not not_11 (not_11_out, in_1);
  not not_12 (not_12_out, d_ff_6_qn);
  D_Flip_Flop d_ff_7 (.clk(not_11_out), .D(not_12_out), .Q(d_ff_9_q[2]), .Qn(d_ff_7_qn));  // open: preset, en, reset
  not not_13 (not_13_out, in_1);
  not not_14 (not_14_out, d_ff_7_qn);
  D_Flip_Flop d_ff_8 (.clk(not_13_out), .D(not_14_out), .Q(d_ff_9_q[1]), .Qn(d_ff_8_qn));  // open: preset, en, reset
  D_Flip_Flop d_ff_9 (.clk(not_15_out), .D(not_16_out), .Q(d_ff_9_q[0]), .Qn(d_ff_9_qn));  // open: preset, en, reset
  not not_15 (not_15_out, in_1);
  not not_16 (not_16_out, d_ff_8_qn);
endmodule

module De_Beauvoir (
  input  [2:0] in_1,
  input  [1:0] in_2,
  output [3:0] out_3,
  output [3:0] out_4,
  output [3:0] out_5,
  output [3:0] out_6
);

  ROM rom_1 (.addr({3'b000, in_2, in_1}), .data({out_5[3:1], out_4[3], out_4[1], out_3[3:1]}));  // open: sel
  or or_1 (out_4[2], out_3[1], out_3[2], out_3[3], out_4[1], out_4[3], out_5[1], out_5[2], out_5[3]);
  and and_1 (out_6[2], ~out_4[3], ~out_5[1], out_5[2], ~out_5[3], ~out_3[1], out_3[2], ~out_3[3], ~out_4[1]);  // AND_Gate
  and and_2 (out_4[0], out_4[3], ~out_5[1], ~out_5[2], ~out_5[3], ~out_3[1], ~out_3[2], ~out_3[3], out_4[1]);  // AND_Gate

  assign out_3[0] = 1'b0;
  assign out_5[0] = 1'b0;
  assign {out_6[3], out_6[1:0]} = 3'b000;

  // Notes on the sheet:
  //   contents of rom_1 (hex, n*v repeats v):
  //   0 13 e 43 46 b 4a 18 0 2a 49 38 19 b 58 42 0 c8 70 c2 62 b 52 18 0 54 92 1c 98 b 1a 42
endmodule

module Rousseaux (
  input  in_1,
  input  [4:0] in_2,
  output _0,
  output _1,
  output _2,
  output _3,
  output _4,
  output _5,
  output _6,
  output _7,
  output _8,
  output _9,
  output _10,
  output _11,
  output _12,
  output _13,
  output _14,
  output _15,
  output _16,
  output _17,
  output _18,
  output _19,
  output _20,
  output _21,
  output _22,
  output _23
);

  wire decoder_1_out0, decoder_1_out1, decoder_1_out2, decoder_1_out3, decoder_1_out4, decoder_1_out5,
       decoder_1_out6, decoder_1_out7, decoder_1_out8, decoder_1_out9, decoder_1_out10, decoder_1_out11,
       decoder_1_out12, decoder_1_out13, decoder_1_out14, decoder_1_out15, decoder_1_out16, decoder_1_out17,
       decoder_1_out18, decoder_1_out19, decoder_1_out20, decoder_1_out21, decoder_1_out22, decoder_1_out23,
       decoder_1_out24, decoder_1_out25, decoder_1_out26, decoder_1_out27, decoder_1_out28, decoder_1_out29,
       decoder_1_out30, decoder_1_out31, or_12_out;

  Decoder #(.select(5), .disabled(0)) decoder_1 (
    .out0(decoder_1_out0), .out1(decoder_1_out1), .out2(decoder_1_out2), .out3(decoder_1_out3),
    .out4(decoder_1_out4), .out5(decoder_1_out5), .out6(decoder_1_out6), .out7(decoder_1_out7),
    .out8(decoder_1_out8), .out9(decoder_1_out9), .out10(decoder_1_out10), .out11(decoder_1_out11),
    .out12(decoder_1_out12), .out13(decoder_1_out13), .out14(decoder_1_out14), .out15(decoder_1_out15),
    .out16(decoder_1_out16), .out17(decoder_1_out17), .out18(decoder_1_out18), .out19(decoder_1_out19),
    .out20(decoder_1_out20), .out21(decoder_1_out21), .out22(decoder_1_out22), .out23(decoder_1_out23),
    .out24(decoder_1_out24), .out25(decoder_1_out25), .out26(decoder_1_out26), .out27(decoder_1_out27),
    .out28(decoder_1_out28), .out29(decoder_1_out29), .out30(decoder_1_out30), .out31(decoder_1_out31),
    .sel(in_2), .en(in_1));
  or or_1 (_23, decoder_1_out24, decoder_1_out25, decoder_1_out26, decoder_1_out27, decoder_1_out28, decoder_1_out29, decoder_1_out30, decoder_1_out31);
  or or_2 (_22, decoder_1_out23, _23);
  or or_3 (_20, decoder_1_out21, _21);
  or or_4 (_21, decoder_1_out22, _22);
  or or_5 (_19, decoder_1_out20, _20);
  or or_6 (_17, decoder_1_out18, _18);
  or or_7 (_18, decoder_1_out19, _19);
  or or_8 (_15, decoder_1_out16, _16);
  or or_9 (_16, decoder_1_out17, _17);
  or or_10 (_14, decoder_1_out15, _15);
  or or_11 (_13, decoder_1_out13, or_12_out);
  or or_12 (or_12_out, decoder_1_out14, _14);
  or or_13 (_12, decoder_1_out12, _13);
  or or_14 (_10, decoder_1_out10, _11);
  or or_15 (_11, decoder_1_out11, _12);
  or or_16 (_8, decoder_1_out8, _9);
  or or_17 (_9, decoder_1_out9, _10);
  or or_18 (_7, decoder_1_out7, _8);
  or or_19 (_5, decoder_1_out5, _6);
  or or_20 (_6, decoder_1_out6, _7);
  or or_21 (_4, decoder_1_out4, _5);
  or or_22 (_2, decoder_1_out2, _3);
  or or_23 (_3, decoder_1_out3, _4);
  or or_24 (_0, decoder_1_out0, _1);
  or or_25 (_1, decoder_1_out1, _2);
endmodule

module D_Artagnan (
  input  [4:0] in_1,
  input  [9:0] in_2,
  input  [9:0] in_3,
  input  [9:0] in_4,
  input  [9:0] in_5,
  input  [9:0] in_6,
  input  [9:0] in_7,
  input  [9:0] in_8,
  input  [9:0] in_9,
  input  [9:0] in_10,
  input  [9:0] in_11,
  input  [9:0] in_12,
  input  [9:0] in_13,
  input  [9:0] in_14,
  input  [9:0] in_15,
  input  [9:0] in_16,
  input  [9:0] in_17,
  input  [9:0] in_18,
  input  [9:0] in_19,
  input  [9:0] in_20,
  input  [9:0] in_21,
  input  [9:0] in_22,
  input  [9:0] in_23,
  input  [9:0] in_24,
  input  [9:0] in_25,
  input  [9:0] in_26,
  output [9:0] out_27,
  output [9:0] out_28,
  output [9:0] out_29,
  output [9:0] out_30,
  output [9:0] out_31,
  output [9:0] out_32,
  output [9:0] out_33,
  output [9:0] out_34,
  output [9:0] out_35,
  output [9:0] out_36,
  output [9:0] out_37,
  output [9:0] out_38,
  output [9:0] out_39,
  output [9:0] out_40,
  output [9:0] out_41,
  output [9:0] out_42,
  output [9:0] out_43,
  output [9:0] out_44,
  output [9:0] out_45,
  output [9:0] out_46,
  output [9:0] out_47,
  output [9:0] out_48,
  output [9:0] out_49,
  output [9:0] out_50
);

  wire [9:0] demultiplexer_1_out0, demultiplexer_1_out1, demultiplexer_1_out2, demultiplexer_1_out3,
       demultiplexer_1_out4, demultiplexer_1_out5, demultiplexer_1_out6, demultiplexer_1_out7,
       demultiplexer_1_out8, demultiplexer_1_out9, demultiplexer_1_out10, demultiplexer_1_out11,
       demultiplexer_1_out12, demultiplexer_1_out13, demultiplexer_1_out14, demultiplexer_1_out15,
       demultiplexer_1_out16, demultiplexer_1_out17, demultiplexer_1_out18, demultiplexer_1_out19,
       demultiplexer_1_out20, demultiplexer_1_out21, demultiplexer_1_out22, demultiplexer_1_out23;

  Demultiplexer #(.select(5), .width(10), .disabled(0)) demultiplexer_1 (
    .out0(demultiplexer_1_out0), .out1(demultiplexer_1_out1), .out2(demultiplexer_1_out2),
    .out3(demultiplexer_1_out3), .out4(demultiplexer_1_out4), .out5(demultiplexer_1_out5),
    .out6(demultiplexer_1_out6), .out7(demultiplexer_1_out7), .out8(demultiplexer_1_out8),
    .out9(demultiplexer_1_out9), .out10(demultiplexer_1_out10), .out11(demultiplexer_1_out11),
    .out12(demultiplexer_1_out12), .out13(demultiplexer_1_out13), .out14(demultiplexer_1_out14),
    .out15(demultiplexer_1_out15), .out16(demultiplexer_1_out16), .out17(demultiplexer_1_out17),
    .out18(demultiplexer_1_out18), .out19(demultiplexer_1_out19), .out20(demultiplexer_1_out20),
    .out21(demultiplexer_1_out21), .out22(demultiplexer_1_out22), .out23(demultiplexer_1_out23), .in(in_2),
    .sel(in_1));  // open: out24, out25, out26, out27, out28, out29, out30, out31, en
  assign out_27 = demultiplexer_1_out0 | in_3;  // OR_Gate or_1, 10 bits wide
  assign out_28 = demultiplexer_1_out1 | in_4;  // OR_Gate or_2, 10 bits wide
  assign out_29 = demultiplexer_1_out2 | in_5;  // OR_Gate or_3, 10 bits wide
  assign out_30 = demultiplexer_1_out3 | in_6;  // OR_Gate or_4, 10 bits wide
  assign out_31 = demultiplexer_1_out4 | in_7;  // OR_Gate or_5, 10 bits wide
  assign out_32 = demultiplexer_1_out5 | in_8;  // OR_Gate or_6, 10 bits wide
  assign out_33 = demultiplexer_1_out6 | in_9;  // OR_Gate or_7, 10 bits wide
  assign out_34 = demultiplexer_1_out7 | in_10;  // OR_Gate or_8, 10 bits wide
  assign out_35 = demultiplexer_1_out8 | in_11;  // OR_Gate or_9, 10 bits wide
  assign out_36 = demultiplexer_1_out9 | in_12;  // OR_Gate or_10, 10 bits wide
  assign out_37 = demultiplexer_1_out10 | in_13;  // OR_Gate or_11, 10 bits wide
  assign out_38 = demultiplexer_1_out11 | in_14;  // OR_Gate or_12, 10 bits wide
  assign out_39 = demultiplexer_1_out12 | in_15;  // OR_Gate or_13, 10 bits wide
  assign out_40 = demultiplexer_1_out13 | in_16;  // OR_Gate or_14, 10 bits wide
  assign out_41 = demultiplexer_1_out14 | in_17;  // OR_Gate or_15, 10 bits wide
  assign out_42 = demultiplexer_1_out15 | in_18;  // OR_Gate or_16, 10 bits wide
  assign out_43 = demultiplexer_1_out16 | in_19;  // OR_Gate or_17, 10 bits wide
  assign out_44 = demultiplexer_1_out17 | in_20;  // OR_Gate or_18, 10 bits wide
  assign out_45 = demultiplexer_1_out18 | in_21;  // OR_Gate or_19, 10 bits wide
  assign out_46 = demultiplexer_1_out19 | in_22;  // OR_Gate or_20, 10 bits wide
  assign out_47 = demultiplexer_1_out20 | in_23;  // OR_Gate or_21, 10 bits wide
  assign out_48 = demultiplexer_1_out21 | in_24;  // OR_Gate or_22, 10 bits wide
  assign out_49 = demultiplexer_1_out22 | in_25;  // OR_Gate or_23, 10 bits wide
  assign out_50 = demultiplexer_1_out23 | in_26;  // OR_Gate or_24, 10 bits wide
endmodule

module Victor_Hugo (
  input  [3:0] in_1,
  input  [3:0] in_2,
  input  [3:0] in_3,
  input  [3:0] in_4,
  input  [3:0] in_5,
  output [9:0] out_6,
  output [9:0] out_7,
  output [9:0] out_8,
  output [9:0] out_9
);

  La_Fontaine la_fontaine_1 ();  // open: in_2, in_3, in_4, in_5, out_6, out_7, out_8, out_9, out_10, out_11, in_1, out_12, out_13
  Shifter #(.width(10), .shift("rl")) shifter_1 (.in({in_1[1:0], {6{1'b0}}, in_1[3:2]}), .\dist (in_5), .out(out_6));
  Shifter #(.width(10), .shift("rl")) shifter_2 (.in({in_2[1:0], {6{1'b0}}, in_2[3:2]}), .\dist (in_5), .out(out_7));
  Shifter #(.width(10), .shift("rl")) shifter_3 (.in({in_3[1:0], {6{1'b0}}, in_3[3:2]}), .\dist (in_5), .out(out_8));
  Shifter #(.width(10), .shift("rl")) shifter_4 (.in({in_4[1:0], {6{1'b0}}, in_4[3:2]}), .\dist (in_5), .out(out_9));
endmodule

module Pagnol (
  input  [9:0] in_1,
  input  [9:0] in_2,
  input  [9:0] in_3,
  input  [9:0] in_4,
  input  [9:0] in_5,
  input  [9:0] in_6,
  input  [9:0] in_7,
  input  [9:0] in_8,
  input  [9:0] in_9,
  input  [3:0] in_10,
  output out_11,
  output out_12,
  output out_13,
  output out_14,
  output out_15,
  output out_16
);

  wire or_12_out;
  wire [9:0] and_17_out, and_18_out, and_19_out, and_20_out, or_1_out, or_2_out, or_3_out, or_4_out,
       or_11_out, or_13_out, xor_1_out, xor_2_out, xor_3_out, xor_4_out;
  wire [13:0] and_1_out, and_2_out, and_3_out, and_4_out, and_5_out, and_6_out, and_7_out, and_8_out,
       and_9_out, and_10_out, and_11_out, and_12_out, and_13_out, and_14_out, and_15_out, and_16_out,
       la_fontaine_1_out_6, la_fontaine_1_out_7, la_fontaine_1_out_8, la_fontaine_1_out_9,
       la_fontaine_1_out_10, la_fontaine_1_out_11, la_fontaine_1_out_12, la_fontaine_1_out_13, or_5_out,
       or_6_out, or_9_out, or_10_out, shifter_1_out, shifter_2_out, shifter_3_out, shifter_4_out,
       shifter_5_out, shifter_6_out, shifter_7_out, shifter_8_out;

  La_Fontaine la_fontaine_1 (
    .in_2(in_4), .in_3(in_3), .in_4(in_2), .in_5(in_1), .out_6(la_fontaine_1_out_6),
    .out_7(la_fontaine_1_out_7), .out_8(la_fontaine_1_out_8), .out_9(la_fontaine_1_out_9),
    .out_10(la_fontaine_1_out_10), .out_11(la_fontaine_1_out_11), .in_1(in_10),
    .out_12(la_fontaine_1_out_12), .out_13(la_fontaine_1_out_13));
  Shifter #(.width(14), .shift("lr")) shifter_1 (.in({2'b00, in_4, 2'b00}), .\dist (4'b0001), .out(shifter_1_out));
  assign and_1_out = shifter_1_out & {2'b11, in_5, 2'b11};  // AND_Gate and_1, 14 bits wide
  Shifter #(.width(14), .shift("lr")) shifter_2 (.in({2'b00, in_3, 2'b00}), .\dist (4'b0001), .out(shifter_2_out));
  assign and_2_out = shifter_2_out & {2'b11, in_6, 2'b11};  // AND_Gate and_2, 14 bits wide
  Shifter #(.width(14), .shift("lr")) shifter_3 (.in({2'b00, in_2, 2'b00}), .\dist (4'b0001), .out(shifter_3_out));
  assign and_3_out = shifter_3_out & {2'b11, in_7, 2'b11};  // AND_Gate and_3, 14 bits wide
  Shifter #(.width(14), .shift("lr")) shifter_4 (.in({2'b00, in_1, 2'b00}), .\dist (4'b0001), .out(shifter_4_out));
  assign and_4_out = shifter_4_out & {2'b11, in_8, 2'b11};  // AND_Gate and_4, 14 bits wide
  Shifter #(.width(14)) shifter_5 (.in({2'b00, in_4, 2'b00}), .\dist (4'b0001), .out(shifter_5_out));
  assign and_5_out = shifter_5_out & {2'b11, in_5, 2'b11};  // AND_Gate and_5, 14 bits wide
  Shifter #(.width(14)) shifter_6 (.in({2'b00, in_3, 2'b00}), .\dist (4'b0001), .out(shifter_6_out));
  assign and_6_out = shifter_6_out & {2'b11, in_6, 2'b11};  // AND_Gate and_6, 14 bits wide
  Shifter #(.width(14)) shifter_7 (.in({2'b00, in_2, 2'b00}), .\dist (4'b0001), .out(shifter_7_out));
  assign and_7_out = shifter_7_out & {2'b11, in_7, 2'b11};  // AND_Gate and_7, 14 bits wide
  Shifter #(.width(14)) shifter_8 (.in({2'b00, in_1, 2'b00}), .\dist (4'b0001), .out(shifter_8_out));
  assign and_8_out = shifter_8_out & {2'b11, in_8, 2'b11};  // AND_Gate and_8, 14 bits wide
  assign or_1_out = in_4 | in_5;  // OR_Gate or_1, 10 bits wide
  assign xor_1_out = or_1_out ^ in_5;  // XOR_Gate xor_1, 10 bits wide
  assign or_2_out = in_3 | in_6;  // OR_Gate or_2, 10 bits wide
  assign xor_2_out = or_2_out ^ in_6;  // XOR_Gate xor_2, 10 bits wide
  assign or_3_out = in_2 | in_7;  // OR_Gate or_3, 10 bits wide
  assign xor_3_out = or_3_out ^ in_7;  // XOR_Gate xor_3, 10 bits wide
  assign or_4_out = in_1 | in_8;  // OR_Gate or_4, 10 bits wide
  assign xor_4_out = or_4_out ^ in_8;  // XOR_Gate xor_4, 10 bits wide
  assign or_5_out = and_1_out | and_2_out | and_3_out | and_4_out;  // OR_Gate or_5, 14 bits wide
  assign or_6_out = and_5_out | and_6_out | and_7_out | and_8_out;  // OR_Gate or_6, 14 bits wide
  assign and_9_out = la_fontaine_1_out_6 & {2'b11, in_5, 2'b11};  // AND_Gate and_9, 14 bits wide
  assign and_10_out = la_fontaine_1_out_7 & {2'b11, in_6, 2'b11};  // AND_Gate and_10, 14 bits wide
  assign and_11_out = la_fontaine_1_out_8 & {2'b11, in_7, 2'b11};  // AND_Gate and_11, 14 bits wide
  assign and_12_out = la_fontaine_1_out_9 & {2'b11, in_8, 2'b11};  // AND_Gate and_12, 14 bits wide
  assign and_13_out = la_fontaine_1_out_10 & {2'b11, in_5, 2'b11};  // AND_Gate and_13, 14 bits wide
  assign and_14_out = la_fontaine_1_out_11 & {2'b11, in_6, 2'b11};  // AND_Gate and_14, 14 bits wide
  assign and_15_out = la_fontaine_1_out_12 & {2'b11, in_7, 2'b11};  // AND_Gate and_15, 14 bits wide
  assign and_16_out = la_fontaine_1_out_13 & {2'b11, in_8, 2'b11};  // AND_Gate and_16, 14 bits wide
  or or_7 (out_12, or_5_out[0], or_5_out[1], or_5_out[2], or_5_out[3], or_5_out[4], or_5_out[5], or_5_out[6], or_5_out[8], or_5_out[9], or_5_out[10], or_5_out[11], or_5_out[12], or_5_out[13], or_5_out[7]);
  or or_8 (out_13, or_6_out[0], or_6_out[1], or_6_out[2], or_6_out[3], or_6_out[4], or_6_out[5], or_6_out[6], or_6_out[8], or_6_out[9], or_6_out[10], or_6_out[11], or_6_out[12], or_6_out[13], or_6_out[7]);
  assign or_9_out = and_9_out | and_10_out | and_11_out | and_12_out;  // OR_Gate or_9, 14 bits wide
  assign or_10_out = and_13_out | and_14_out | and_15_out | and_16_out;  // OR_Gate or_10, 14 bits wide
  assign or_11_out = xor_2_out | xor_1_out | xor_4_out | xor_3_out;  // OR_Gate or_11, 10 bits wide
  assign and_17_out = in_6 & in_4;  // AND_Gate and_17, 10 bits wide
  assign and_18_out = in_7 & in_3;  // AND_Gate and_18, 10 bits wide
  assign and_19_out = in_8 & in_2;  // AND_Gate and_19, 10 bits wide
  assign and_20_out = in_9 & in_1;  // AND_Gate and_20, 10 bits wide
  or or_12 (or_12_out, or_11_out[0], or_11_out[1], or_11_out[2], or_11_out[3], or_11_out[4], or_11_out[6], or_11_out[7], or_11_out[8], or_11_out[9], or_11_out[5]);
  not not_1 (out_16, or_12_out);
  assign or_13_out = and_17_out | and_18_out | and_19_out | and_20_out;  // OR_Gate or_13, 10 bits wide
  or or_14 (out_14, or_9_out[0], or_9_out[1], or_9_out[2], or_9_out[3], or_9_out[4], or_9_out[5], or_9_out[6], or_9_out[8], or_9_out[9], or_9_out[10], or_9_out[11], or_9_out[12], or_9_out[13], or_9_out[7]);
  or or_15 (out_15, or_10_out[0], or_10_out[1], or_10_out[2], or_10_out[3], or_10_out[4], or_10_out[5], or_10_out[6], or_10_out[8], or_10_out[9], or_10_out[10], or_10_out[11], or_10_out[12], or_10_out[13], or_10_out[7]);
  or or_16 (out_11, or_13_out[0], or_13_out[1], or_13_out[2], or_13_out[3], or_13_out[4], or_13_out[6], or_13_out[7], or_13_out[8], or_13_out[9], or_13_out[5]);
endmodule

module Baudelaire (
  input  [9:0] in_1,
  input  [9:0] in_2,
  input  [9:0] in_3,
  input  [9:0] in_4,
  input  [9:0] in_5,
  input  [9:0] in_6,
  input  [9:0] in_7,
  input  [9:0] in_8,
  input  [9:0] in_9,
  input  [9:0] in_10,
  input  [9:0] in_11,
  input  [9:0] in_12,
  input  [9:0] in_13,
  input  [9:0] in_14,
  input  [9:0] in_15,
  input  [9:0] in_16,
  input  [9:0] in_17,
  input  [9:0] in_18,
  input  [9:0] in_19,
  input  [9:0] in_20,
  input  [9:0] in_21,
  input  [9:0] in_22,
  input  [9:0] in_23,
  input  [9:0] in_24,
  input  [4:0] in_25,
  output out_26,
  output [9:0] out_27,
  output [9:0] out_28,
  output [9:0] out_29,
  output [9:0] out_30,
  output [9:0] out_31,
  output [9:0] out_32,
  output [9:0] out_33,
  output [9:0] out_34,
  output [9:0] out_35,
  output [9:0] out_36,
  output [9:0] out_37,
  output [9:0] out_38,
  output [9:0] out_39,
  output [9:0] out_40,
  output [9:0] out_41,
  output [9:0] out_42,
  output [9:0] out_43,
  output [9:0] out_44,
  output [9:0] out_45,
  output [9:0] out_46,
  output [9:0] out_47,
  output [9:0] out_48,
  output [9:0] out_49,
  output [9:0] out_50,
  output [9:0] out_51,
  output [9:0] out_52,
  output [9:0] out_53,
  output [9:0] out_54,
  output [9:0] out_55,
  output out_56,
  output [4:0] out_57
);

  wire alfred_alfred_1_out_2, alfred_alfred_2_out_2, alfred_alfred_3_out_2, alfred_alfred_4_out_2,
       alfred_alfred_5_out_2, alfred_alfred_6_out_2, alfred_alfred_7_out_2, alfred_alfred_8_out_2,
       alfred_alfred_9_out_2, alfred_alfred_10_out_2, alfred_alfred_11_out_2, alfred_alfred_12_out_2,
       alfred_alfred_13_out_2, alfred_alfred_14_out_2, alfred_alfred_15_out_2, alfred_alfred_16_out_2,
       alfred_alfred_17_out_2, alfred_alfred_18_out_2, alfred_alfred_19_out_2, alfred_alfred_20_out_2,
       alfred_alfred_21_out_2, alfred_alfred_22_out_2, alfred_alfred_23_out_2, alfred_alfred_24_out_2,
       camus_1_out_2, camus_2_out_2, camus_3_out_2, camus_4_out_2;
  wire [4:0] adder_1_out, adder_2_out, subtractor_1_out, subtractor_2_out;

  Adder #(.width(5)) adder_1 (.a(adder_2_out), .b({5{1'b0}}), .out(adder_1_out), .cin(1'b1));  // open: cout
  Multiplexer #(.select(5), .width(10), .disabled(0), .enable("false")) multiplexer_1 (
    .in0(in_1), .in1(in_2), .in2(in_3), .in3(in_4), .in4(in_5), .in5(in_6), .in6(in_7), .in7(in_8),
    .in8(in_9), .in9(in_10), .in10(in_11), .in11(in_12), .in12(in_13), .in13(in_14), .in14(in_15),
    .in15(in_16), .in16(in_17), .in17(in_18), .in18(in_19), .in19(in_20), .in20(in_21), .in21(in_22),
    .in22(in_23), .in23(in_24), .in24({10{1'b1}}), .in25({10{1'b1}}), .in26({10{1'b1}}), .in27({10{1'b1}}),
    .in28({10{1'b1}}), .in29({10{1'b1}}), .in30({10{1'b1}}), .in31({10{1'b1}}), .out(out_51),
    .sel(adder_1_out));
  Adder #(.width(5)) adder_2 (.a(in_25), .b({5{1'b0}}), .out(adder_2_out), .cin(1'b1));  // open: cout
  Multiplexer #(.select(5), .width(10), .disabled(0), .enable("false")) multiplexer_2 (
    .in0(in_1), .in1(in_2), .in2(in_3), .in3(in_4), .in4(in_5), .in5(in_6), .in6(in_7), .in7(in_8),
    .in8(in_9), .in9(in_10), .in10(in_11), .in11(in_12), .in12(in_13), .in13(in_14), .in14(in_15),
    .in15(in_16), .in16(in_17), .in17(in_18), .in18(in_19), .in19(in_20), .in20(in_21), .in21(in_22),
    .in22(in_23), .in23(in_24), .in24({10{1'b1}}), .in25({10{1'b1}}), .in26({10{1'b1}}), .in27({10{1'b1}}),
    .in28({10{1'b1}}), .in29({10{1'b1}}), .in30({10{1'b1}}), .in31({10{1'b1}}), .out(out_52),
    .sel(adder_2_out));
  Multiplexer #(.select(5), .width(10), .disabled(0), .enable("false")) multiplexer_3 (
    .in0(in_1), .in1(in_2), .in2(in_3), .in3(in_4), .in4(in_5), .in5(in_6), .in6(in_7), .in7(in_8),
    .in8(in_9), .in9(in_10), .in10(in_11), .in11(in_12), .in12(in_13), .in13(in_14), .in14(in_15),
    .in15(in_16), .in16(in_17), .in17(in_18), .in18(in_19), .in19(in_20), .in20(in_21), .in21(in_22),
    .in22(in_23), .in23(in_24), .in24({10{1'b1}}), .in25({10{1'b1}}), .in26({10{1'b1}}), .in27({10{1'b1}}),
    .in28({10{1'b1}}), .in29({10{1'b1}}), .in30({10{1'b1}}), .in31({10{1'b1}}), .out(out_53), .sel(in_25));
  Subtractor #(.width(5)) subtractor_1 (.a(in_25), .b({5{1'b0}}), .out(subtractor_1_out), .bin(1'b1));  // open: bout
  Multiplexer #(.select(5), .width(10), .disabled(0), .enable("false")) multiplexer_4 (
    .in0(in_1), .in1(in_2), .in2(in_3), .in3(in_4), .in4(in_5), .in5(in_6), .in6(in_7), .in7(in_8),
    .in8(in_9), .in9(in_10), .in10(in_11), .in11(in_12), .in12(in_13), .in13(in_14), .in14(in_15),
    .in15(in_16), .in16(in_17), .in17(in_18), .in18(in_19), .in19(in_20), .in20(in_21), .in21(in_22),
    .in22(in_23), .in23(in_24), .in24({10{1'b1}}), .in25({10{1'b1}}), .in26({10{1'b1}}), .in27({10{1'b1}}),
    .in28({10{1'b1}}), .in29({10{1'b1}}), .in30({10{1'b1}}), .in31({10{1'b1}}), .out(out_54),
    .sel(subtractor_1_out));
  Subtractor #(.width(5)) subtractor_2 (
    .a(subtractor_1_out), .b({5{1'b0}}), .out(subtractor_2_out), .bin(1'b1));  // open: bout
  Multiplexer #(.select(5), .width(10), .disabled(0), .enable("false")) multiplexer_5 (
    .in0(in_1), .in1(in_2), .in2(in_3), .in3(in_4), .in4(in_5), .in5(in_6), .in6(in_7), .in7(in_8),
    .in8(in_9), .in9(in_10), .in10(in_11), .in11(in_12), .in12(in_13), .in13(in_14), .in14(in_15),
    .in15(in_16), .in16(in_17), .in17(in_18), .in18(in_19), .in19(in_20), .in20(in_21), .in21(in_22),
    .in22(in_23), .in23(in_24), .in24({10{1'b1}}), .in25({10{1'b1}}), .in26({10{1'b1}}), .in27({10{1'b1}}),
    .in28({10{1'b1}}), .in29({10{1'b1}}), .in30({10{1'b1}}), .in31({10{1'b1}}), .out(out_55),
    .sel(subtractor_2_out));
  Alfred___Alfred alfred_alfred_1 (.in_1(in_1), .out_2(alfred_alfred_1_out_2));
  Alfred___Alfred alfred_alfred_2 (.in_1(in_3), .out_2(alfred_alfred_2_out_2));
  Alfred___Alfred alfred_alfred_3 (.in_1(in_6), .out_2(alfred_alfred_3_out_2));
  Alfred___Alfred alfred_alfred_4 (.in_1(in_4), .out_2(alfred_alfred_4_out_2));
  Alfred___Alfred alfred_alfred_5 (.in_1(in_2), .out_2(alfred_alfred_5_out_2));
  Alfred___Alfred alfred_alfred_6 (.in_1(in_7), .out_2(alfred_alfred_6_out_2));
  Alfred___Alfred alfred_alfred_7 (.in_1(in_5), .out_2(alfred_alfred_7_out_2));
  Alfred___Alfred alfred_alfred_8 (.in_1(in_12), .out_2(alfred_alfred_8_out_2));
  Alfred___Alfred alfred_alfred_9 (.in_1(in_14), .out_2(alfred_alfred_9_out_2));
  Alfred___Alfred alfred_alfred_10 (.in_1(in_10), .out_2(alfred_alfred_10_out_2));
  Alfred___Alfred alfred_alfred_11 (.in_1(in_11), .out_2(alfred_alfred_11_out_2));
  Alfred___Alfred alfred_alfred_12 (.in_1(in_8), .out_2(alfred_alfred_12_out_2));
  Alfred___Alfred alfred_alfred_13 (.in_1(in_13), .out_2(alfred_alfred_13_out_2));
  Alfred___Alfred alfred_alfred_14 (.in_1(in_9), .out_2(alfred_alfred_14_out_2));
  Alfred___Alfred alfred_alfred_15 (.in_1(in_15), .out_2(alfred_alfred_15_out_2));
  Alfred___Alfred alfred_alfred_16 (.in_1(in_21), .out_2(alfred_alfred_16_out_2));
  Alfred___Alfred alfred_alfred_17 (.in_1(in_17), .out_2(alfred_alfred_17_out_2));
  Alfred___Alfred alfred_alfred_18 (.in_1(in_18), .out_2(alfred_alfred_18_out_2));
  Alfred___Alfred alfred_alfred_19 (.in_1(in_22), .out_2(alfred_alfred_19_out_2));
  Alfred___Alfred alfred_alfred_20 (.in_1(in_19), .out_2(alfred_alfred_20_out_2));
  Alfred___Alfred alfred_alfred_21 (.in_1(in_23), .out_2(alfred_alfred_21_out_2));
  Alfred___Alfred alfred_alfred_22 (.in_1(in_20), .out_2(alfred_alfred_22_out_2));
  Alfred___Alfred alfred_alfred_23 (.in_1(in_16), .out_2(alfred_alfred_23_out_2));
  Camus camus_1 (.in_1(in_1), .out_2(camus_1_out_2));
  Camus camus_2 (.in_1(in_2), .out_2(camus_2_out_2));
  or or_1 (out_26, camus_1_out_2, camus_2_out_2, camus_3_out_2, camus_4_out_2);
  Camus camus_3 (.in_1(in_3), .out_2(camus_3_out_2));
  Camus camus_4 (.in_1(in_4), .out_2(camus_4_out_2));
  Alfred___Alfred alfred_alfred_24 (.in_1(in_24), .out_2(alfred_alfred_24_out_2));
  Priority_Encoder #(.select(5), .disabled(0)) priority_encoder_1 (
    .in0(1'b1), .in1(alfred_alfred_1_out_2), .in2(alfred_alfred_5_out_2), .in3(alfred_alfred_2_out_2),
    .in4(alfred_alfred_4_out_2), .in5(alfred_alfred_7_out_2), .in6(alfred_alfred_3_out_2),
    .in7(alfred_alfred_6_out_2), .in8(alfred_alfred_12_out_2), .in9(alfred_alfred_14_out_2),
    .in10(alfred_alfred_10_out_2), .in11(alfred_alfred_11_out_2), .in12(alfred_alfred_8_out_2),
    .in13(alfred_alfred_13_out_2), .in14(alfred_alfred_9_out_2), .in15(alfred_alfred_15_out_2),
    .in16(alfred_alfred_23_out_2), .in17(alfred_alfred_17_out_2), .in18(alfred_alfred_18_out_2),
    .in19(alfred_alfred_20_out_2), .in20(alfred_alfred_22_out_2), .in21(alfred_alfred_16_out_2),
    .in22(alfred_alfred_19_out_2), .in23(alfred_alfred_21_out_2), .in24(alfred_alfred_24_out_2), .in25(1'b0),
    .in26(1'b0), .in27(1'b0), .in28(1'b0), .in29(1'b0), .in30(1'b0), .in31(1'b0), .out(out_57));  // open: gs, en_out, en_in
  or or_2 (out_56, out_57[4], out_57[3], out_57[2], out_57[1], out_57[0]);

  assign out_27 = in_1;
  assign out_28 = in_2;
  assign out_29 = in_3;
  assign out_30 = in_4;
  assign out_31 = in_5;
  assign out_32 = in_6;
  assign out_33 = in_7;
  assign out_34 = in_8;
  assign out_35 = in_9;
  assign out_36 = in_10;
  assign out_37 = in_11;
  assign out_38 = in_12;
  assign out_39 = in_13;
  assign out_40 = in_14;
  assign out_41 = in_15;
  assign out_42 = in_16;
  assign out_43 = in_17;
  assign out_44 = in_18;
  assign out_45 = in_19;
  assign out_46 = in_20;
  assign out_47 = in_21;
  assign out_48 = in_22;
  assign out_49 = in_23;
  assign out_50 = in_24;
endmodule

module La_Fontaine (
  input  [3:0] in_1,
  input  [9:0] in_2,
  input  [9:0] in_3,
  input  [9:0] in_4,
  input  [9:0] in_5,
  output [13:0] out_6,
  output [13:0] out_7,
  output [13:0] out_8,
  output [13:0] out_9,
  output [13:0] out_10,
  output [13:0] out_11,
  output [13:0] out_12,
  output [13:0] out_13
);

  wire [9:0] shifter_1_out, shifter_2_out, shifter_3_out, shifter_4_out;

  Shifter #(.width(10), .shift("rr")) shifter_1 (.in(in_2), .\dist (in_1), .out(shifter_1_out));
  Shifter #(.width(10), .shift("rr")) shifter_2 (.in(in_3), .\dist (in_1), .out(shifter_2_out));
  Shifter #(.width(10), .shift("rr")) shifter_3 (.in(in_4), .\dist (in_1), .out(shifter_3_out));
  Shifter #(.width(10), .shift("rr")) shifter_4 (.in(in_5), .\dist (in_1), .out(shifter_4_out));
  Shifter #(.width(14), .shift("rl")) shifter_5 (
    .in({{10{1'b0}}, shifter_1_out[1], shifter_3_out[8], shifter_1_out[9:8]}), .\dist (in_1), .out(out_6));
  Shifter #(.width(14), .shift("rl")) shifter_6 (
    .in({{10{1'b0}}, shifter_4_out[1], shifter_3_out[1], shifter_2_out[1], shifter_2_out[8]}), .\dist (in_1),
    .out(out_7));
  Shifter #(.width(14), .shift("rl")) shifter_7 (
    .in({{10{1'b0}}, shifter_4_out[0], shifter_3_out[0], shifter_2_out[0], shifter_1_out[0]}), .\dist (in_1),
    .out(out_8));
  Shifter #(.width(14), .shift("rl")) shifter_8 (
    .in({{10{1'b0}}, shifter_4_out[9], shifter_3_out[9], shifter_2_out[9], shifter_4_out[8]}), .\dist (in_1),
    .out(out_9));
  Shifter #(.width(14), .shift("rl")) shifter_9 (
    .in({{10{1'b0}}, shifter_1_out[1], shifter_3_out[8], shifter_1_out[9:8]}), .\dist (in_1), .out(out_10));
  Shifter #(.width(14), .shift("rl")) shifter_10 (
    .in({{10{1'b0}}, shifter_2_out[9], shifter_3_out[9], shifter_4_out[9], shifter_2_out[8]}), .\dist (in_1),
    .out(out_11));
  Shifter #(.width(14), .shift("rl")) shifter_11 (
    .in({{10{1'b0}}, shifter_2_out[0], shifter_3_out[0], shifter_4_out[0], shifter_1_out[0]}), .\dist (in_1),
    .out(out_12));
  Shifter #(.width(14), .shift("rl")) shifter_12 (
    .in({{10{1'b0}}, shifter_2_out[1], shifter_3_out[1], shifter_4_out[1], shifter_4_out[8]}), .\dist (in_1),
    .out(out_13));
endmodule

module Camus (
  input  [9:0] in_1,
  output out_2
);

  or or_1 (out_2, in_1[0], in_1[1], in_1[2], in_1[3], in_1[4], in_1[6], in_1[7], in_1[8], in_1[9], in_1[5]);
endmodule

module Alfred___Alfred (
  input  [9:0] in_1,
  output out_2
);

  and and_1 (out_2, in_1[0], in_1[1], in_1[2], in_1[3], in_1[4], in_1[6], in_1[7], in_1[8], in_1[9], in_1[5]);
endmodule

module Proust (
  input  in_1,
  input  in_2,
  input  in_3,
  input  in_4,
  input  in_5,
  input  in_6,
  input  in_7,
  input  in_8,
  input  in_9,
  input  in_10,
  input  in_11,
  input  in_12,
  output [4:0] out_13,
  output [1:0] out_14,
  output [3:0] out_15
);

  wire and_1_out, and_2_out, and_3_out, and_4_out, and_5_out, not_1_out, or_1_out, or_2_out, or_3_out,
       or_4_out;
  wire [4:0] counter_3_q;

  or or_1 (or_1_out, in_7, in_8);
  and and_1 (and_1_out, in_2, ~in_3);  // AND_Gate
  and and_2 (and_2_out, in_1, ~in_4);  // AND_Gate
  and and_3 (and_3_out, in_10, ~in_11);  // AND_Gate
  and and_4 (and_4_out, in_9, ~in_12);  // AND_Gate
  Counter #(.width(2), .max('h3)) counter_1 (
    .load(and_1_out), .Q(out_14), .clk(or_2_out), .clr(in_7));  // open: D, count, carry
  or or_2 (or_2_out, and_1_out, and_2_out);
  or or_3 (or_3_out, or_1_out, and_3_out);
  not not_1 (not_1_out, or_1_out);
  or or_4 (or_4_out, and_3_out, or_1_out, and_4_out);
  Counter #(.width(4), .max('h9)) counter_2 (
    .load(or_3_out), .D(4'b0100), .count(not_1_out), .Q(out_15), .clk(or_4_out));  // open: carry, clr
  Counter #(.width(5), .max('h18), .ongoal("load")) counter_3 (
    .Q(counter_3_q), .clk(and_5_out), .clr(or_1_out));  // open: load, D, count, carry
  and and_5 (and_5_out, in_5, ~in_6);  // AND_Gate
  Adder #(.width(5)) adder_1 (.a(counter_3_q), .b(5'b00010), .out(out_13));  // open: cin, cout
endmodule

module Flaubert (
  input  in_1,
  input  in_2,
  input  in_3,
  output [15:0] out_4,
  output out_5,
  output out_6
);

  wire [15:0] adder_1_out;

  Register #(.width(16)) register_1 (.D(adder_1_out), .en(in_1), .Q(out_4), .clk(in_2), .clr(in_3));
  Adder #(.width(16)) adder_1 (.a(out_4), .b(16'h5), .out(adder_1_out), .cout(out_5));  // open: cin
  and and_1 (out_6, out_4[0], ~out_4[1], ~out_4[2], out_4[3], out_4[4], ~out_4[5], ~out_4[6], out_4[7], ~out_4[9], ~out_4[10], out_4[11], out_4[12], ~out_4[13], ~out_4[14], out_4[15], out_4[8]);  // AND_Gate
endmodule

module Zola (
  input  in_1,
  input  in_2,
  input  [15:0] patterne,
  input  in_4,
  input  [15:0] Key,
  input  in_6,
  input  in_7,
  input  in_8,
  input  in_9,
  output [2:0] out_10,
  output out_11,
  output out_12,
  output out_13,
  output out_14,
  output out_15,
  output out_16,
  output out_17
);

  wire and_2_out, bitselector_1_out, decoder_1_out4, multiplexer_1_out, multiplexer_2_out, nor_1_out,
       not_1_out, or_1_out, or_2_out, or_3_out;
  wire [2:0] random_1_out;
  wire [3:0] decoder_1_out0, multiplexer_5_out;
  wire [7:0] multiplexer_3_out, rom_1_data, xor_1_out;
  wire [10:0] counter_1_q;

  not not_1 (not_1_out, in_1);
  Multiplexer #(.enable("false")) multiplexer_1 (.in0(1'b0), .in1(not_1_out), .out(multiplexer_1_out), .sel(and_2_out));
  Counter #(.width(11), .max('h7ff)) counter_1 (
    .Q(counter_1_q), .clk(multiplexer_1_out));  // open: load, D, count, carry, clr
  BitSelector #(.width(16)) bitselector_1 (.in(patterne), .out(bitselector_1_out), .sel(counter_1_q[3:0]));
  Multiplexer #(.enable("false")) multiplexer_2 (.in0(in_1), .in1(in_2), .out(multiplexer_2_out), .sel(or_1_out));
  or or_1 (or_1_out, random_1_out[0], random_1_out[1], random_1_out[2]);
  Random #(.width(3), .trigger("falling")) random_1 (.clk(multiplexer_2_out), .out(random_1_out));  // open: next, clr
  ROM #(.addrWidth(11)) rom_1 (.addr(counter_1_q), .data(rom_1_data));  // open: sel
  assign xor_1_out = rom_1_data ^ multiplexer_3_out;  // XOR_Gate xor_1, 8 bits wide
  Multiplexer #(.width(8), .disabled(0), .enable("false")) multiplexer_3 (
    .in0(Key[7:0]), .in1(Key[15:8]), .out(multiplexer_3_out), .sel(bitselector_1_out));
  Decoder #(.select(3), .disabled(0), .enable("false")) decoder_1 (
    .out0(decoder_1_out0[0]), .out1(decoder_1_out0[1]), .out2(decoder_1_out0[2]), .out3(decoder_1_out0[3]),
    .out4(decoder_1_out4), .out7(decoder_1_out4), .sel(xor_1_out[4:2]));  // open: out5, out6
  and and_1 (out_14, xor_1_out[0], nor_1_out);
  nor nor_1 (nor_1_out, xor_1_out[1], xor_1_out[2], xor_1_out[3], xor_1_out[4], xor_1_out[5], xor_1_out[6], xor_1_out[7]);
  or or_2 (or_2_out, rom_1_data[0], or_3_out);
  or or_3 (or_3_out, rom_1_data[1], rom_1_data[2], rom_1_data[3], rom_1_data[4], rom_1_data[5], rom_1_data[6], rom_1_data[7]);
  Multiplexer #(.width(3), .disabled(0), .enable("false")) multiplexer_4 (
    .in0(random_1_out), .in1(xor_1_out[7:5]), .out(out_10), .sel(and_2_out));
  Multiplexer #(.width(4), .disabled(0), .enable("false")) multiplexer_5 (
    .in0(decoder_1_out0), .in1(4'b0000), .out(multiplexer_5_out), .sel(multiplexer_1_out));
  Multiplexer #(.disabled(0), .enable("false")) multiplexer_6 (
    .in0(1'b0), .in1(xor_1_out[1]), .out(out_11), .sel(and_2_out));
  Multiplexer #(.disabled(0), .enable("false")) multiplexer_7 (
    .in0(1'b0), .in1(xor_1_out[0]), .out(out_12), .sel(and_2_out));
  Multiplexer #(.width(4), .disabled(0), .enable("false")) multiplexer_8 (
    .in0({in_9, in_8, in_7, in_6}), .in1(multiplexer_5_out), .out({out_17, out_16, out_15, out_13}),
    .sel(and_2_out));
  and and_2 (and_2_out, in_4, or_2_out);

  // Notes on the sheet:
  //   contents of rom_1 (hex, n*v repeats v):
  //   d3 46 46 d2 d2 46 46 d2 d2 46 46 d2 d2 46 46 d2 d2 46 46 d2 d2 46 46 d2 d2 46 46 d2 d2 46 46 d2 f 9b
  //   9b f f 9b 9b f f 9b 9b 1b 7 93 93 7 7 93 9b f d bf bb 2f 2f bb bb 3f 3f b7 b7 23 23 b7 b7 23 23 b7
  //   b7 23 25 b3 b3 27 33 bf bf 2b 2b ab ab 27 27 b3 b3 27 27 bb bd 23 23 b7 b7 23 23 b7 b7 23 23 a7 bb
  //   3f 2e ba ba 2e 2e ba bf 29 2b bf bf 2b 2b bf bf 2b 2b bf a7 3b 2b bf bf 2b 2b bf b9 27 27 b3 b3 27
  //   27 b3 b3 27 27 ab ab 23 23 b7 b7 23 2f bd b3 27 27 b3 b3 27 27 b3 b3 27 33 bb ab 27 27 b9 93 3 3 97
  //   97 3 3 97 97 3 3 8f 9e a a 9e 9e a f 91 b7 23 23 b7 b7 23 23 b7 b7 23 23 ab ab 23 23 b7 b7 23 2f b9
  //   bb 2f 2f bb bb 2f 2f bb bb 2f 33 ab ab 27 27 b3 b3 25 23 b7 b7 23 23 b7 b7 23 23 b7 a7 23 3f b2 b2
  //   26 26 b2 b2 2b 21 bb bb 2f 2f bb bb 2f 2f bb bb 33 3f ab b7 23 23 bf bf 2d 23 b7 b7 23 23 b7 b7 23
  //   23 b7 a7 2f 3f bb bb 29 6f fb fb 6f 6f fb fb 6f 6f fb fb 7f 6a fe fe 6a 6a fe f3 61 63 f7 f7 63 63
  //   f7 f7 63 63 f7 eb 63 63 f7 f7 63 6f f5 33 af af 3b 3b af af 3b 3b af af 27 27 b3 bb 35 d3 4f 4f db
  //   c7 53 4f cb cb 43 43 d7 d7 43 4b dd f3 67 67 f3 f3 67 67 eb eb 7f 6f fb f2 66 66 f2 f2 66 6f fd bb
  //   2b 2b bf bf 2b 2b bf ab 3f 3f b7 b7 23 23 b7 b7 21 b 9b 9b f f 9b 83 7 1f 8b 9f b b 9f 9f f f 95 b3
  //   2b 2b bf bf 2b 2f bb bb 2f 2f ab bf 2b 2b b5 7b ef ef 7b 7b ef ef 7b 7b ef ef 7a 7a ee ee 7a 7a ef
  //   ef 79 9f 7 7 93 93 7 7 93 87 13 1f 9b 9b f f 97 97 1 8b 1f 1f 8b 8b 1f 1f 8b 8b 1f 1f 8f 8f 1b 1b 81
  //   27 b3 b3 27 27 a7 ab 3f 3f ab ba 2e 2e ba ba 2e 22 bb bb 29 27 b3 b3 27 27 b3 b3 27 27 b3 af 3b 23
  //   b7 b7 23 23 b7 b7 21 eb 77 77 e3 ef 7b 7b fb fb 73 73 e7 e7 73 77 e3 ed 13 1b 8f 8f 1b 1b 8f 9f b b
  //   87 87 13 13 8b 8b 1d 97 7 7 93 93 7 7 93 93 7 7 8b 9f b b 9f 9f 5 b 9f 9f b b 9f 9f b b 9f 87 1b 6
  //   92 92 6 6 92 97 9 2f b7 b7 23 23 b7 b7 23 23 b7 b7 3f 3f bf bf 2b 2b bf b3 29 23 b7 b7 23 23 b7 b7
  //   23 23 b7 ab 3f 23 a7 b3 27 27 b1 bb 2f 2f bb bb 2f 2f bb bb 2f 33 ab b6 22 22 b6 b6 22 27 b3 b9 2f
  //   2f bb bb 2f 2f bb bb 2f 2f a7 b7 3f 3f b3 b3 2b 29 db d3 47 47 d3 d3 47 47 d3 d3 47 53 c7 df 4b 4b
  //   df d3 49 4f db db 4f 4f db db 4f 4f db d3 47 47 d3 d7 41 e3 7b 7b ef ef 7b 7b ef ef 6b 6b e2 e2 76
  //   76 e2 e2 73 75 ef eb 7b 7f ef e3 73 73 ef e7 73 7f eb eb 73 77 e9 2f bf bf 2f 2b b3 b7 33 3f bb bf
  //   2b 3f b7 b7 2d ab 33 37 ab ab 33 3b a7 b7 3f 3b a3 a7 3e 32 aa aa 3e 36 ab a9 df d7 4f 47 d3 d7 4f
  //   4b c7 cb 5f 4b db d3 47 4b db d3 47 45 33 37 af a7 3f 33 a7 b3 27 3b a7 bf 2b 3f ab a7 39 d7 4f 4f
  //   db d7 4f 47 df db 53 47 db d7 4b 47 d5 df 4b 4b df d3 47 4b d7 c7 5f 5f d7 d6 46 4e d2 de 4e 4b d5
  //   df 43 43 d7 d7 4b 4f d3 df 4b 5f cb cb 4f 5b db dd 8b 8b 1b 13 87 8f 13 13 87 87 7 f 9b 8b 1f 13 9f
  //   83 1b 15 ab a3 3f 3f a7 a3 3f 3b b3 b3 27 2f af a7 3b 3b a5 23 b3 b7 2f 2b b7 bb 2f 2f b7 bf 3f 26
  //   b6 ba 2a 22 be b7 2f 29 3b 3f af b3 27 27 b3 b3 27 27 b3 b3 27 33 bf bf 3a 37 ab a1 df d7 4b 43 c7
  //   c7 5f 5f cb d3 43 5b cf c3 5b 57 cf db 43 45 db d7 4f 4b db db 43 4b db df 53 53 d3 cb 5f 4b dd 3b
  //   a7 a7 37 3f a7 a7 37 37 bb bb 37 2b a3 a7 37 31 3 7 97 87 13 13 87 87 1b 1f 8b 9a 6 2 9e 9e 6 3 9b
  //   95 87 9b f b 9f 9f f f 9b 9f b b 9f 9f f 1f 87 81 7f 6f fb ff 6b 6b ff fb 6f 6f fb ff 6b 6f fb ff 73
  //   79 4f 47 d3 df 4b 4f d3 d3 4b 4f df cb 43 4a da d6 46 42 d2 d7 49 ab 3b 3b a7 af 3f 33 a3 a7 37 37
  //   b3 b3 27 2f a3 af 37 37 a1 47 d3 db 4f 47 d3 d3 43 4f df df 53 53 cf db 4b 4d 37 3b ab a7 27 33 b3
  //   b3 27 23 af bf 3f 3f a7 a1 df d7 4f 43 d7 db 4b 43 db c3 5f 5f d6 de 4e 4a d2 d6 43 4d 1b 13 83 93 7
  //   7 93 93 7 7 93 93 f f 8f 83 b 13 8f 85 3f 3b a3 ab 2b 2f bf bb 27 27 b3 b3 23 2f a7 af 3d d3 47 43
  //   d3 d3 47 43 cb cb 5f 5f cf cf 47 43 d3 d5 63 6f fb ff 63 6b f7 f7 67 7f eb eb 66 6e f2 fe 6a 6e fb
  //   fd 2b 3f a7 a7 33 33 a7 a7 33 33 a7 af 3f 3f ab b7 2b 21 93 9b b 7 9b 93 3 13 9f 9b 3 7 8b 8b f f 9f
  //   9d 2f 3f bb b3 2b 2f bb b7 2f 2f bf bb 2f 23 bb b5 27 2f b7 bb 23 27 bf bf 23 2f ab bf 23 2a ba b2
  //   2a 2a ba b7 29 2f b7 bb 23 2b bf bf 2f 23 bf a7 3f 3f bb b3 27 2f bb bd a7 af 3b 37 af af 3b 3f a3
  //   a7 33 33 a3 a6 36 3a a2 ae 3e 33 a5 a7 3f 3f ab ab 37 27 bb bb 3f 3f ab bf 37 3b a3 af 3d 37 af ab
  //   37 3f af b3 27 2b bf bf 3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
endmodule

module Verlaine (
  input  [15:0] in_1,
  input  in_2,
  output [3:0] out_3,
  output [3:0] out_4,
  output [3:0] out_5,
  output [3:0] out_6,
  output out_7
);


  assign out_3 = in_1[15:12];
  assign out_4 = in_1[11:8];
  assign out_5 = in_1[7:4];
  assign out_6 = in_1[3:0];
  assign out_7 = in_2;
endmodule

module Corneille (
  input  in_1,
  input  in_2,
  output out_3,
  output out_4
);

  wire d_ff_1_q, or_1_out;

  or or_1 (or_1_out, in_1, d_ff_1_q);
  D_Flip_Flop d_ff_1 (.clk(in_2), .D(or_1_out), .Q(d_ff_1_q));  // open: Qn, preset, en, reset
  and and_1 (out_3, in_1, ~d_ff_1_q);  // AND_Gate
  and and_2 (out_4, in_2, d_ff_1_q);
endmodule
